// Logisim project New_AddSub.circ as structural Verilog: 3 circuits, main circuit main
module main (
  input  in_1,
  input  [7:0] A,
  input  [7:0] B,
  output [7:0] out_4,
  output [7:0] out_5,
  output [7:0] out_6,
  output [7:0] out_7
);

  wire adder_1_cout, adder_2_cout, adder_3_cout, adder_4_cout, comparator_1_eq, comparator_2_eq,
       comparator_3_eq, comparator_4_eq, subtractor_1_bout;
  wire [7:0] negator_1_out, negator_2_out, not_1_out;

  Adder adder_1 (.a(A), .b(B), .cout(adder_1_cout));  // open: out, cin
  Negator negator_1 (.in(B), .out(negator_1_out));
  assign not_1_out = ~B;  // NOT_Gate not_1, 8 bits wide
  Negator negator_2 (.in(B), .out(negator_2_out));
  LED led_1 (.in(adder_1_cout));
  Subtractor subtractor_1 (.a(A), .b(B), .out(out_4), .bin(in_1), .bout(subtractor_1_bout));
  LED led_2 (.in(subtractor_1_bout));
  Adder adder_2 (.a(A), .b(negator_1_out), .out(out_5), .cout(adder_2_cout));  // open: cin
  LED led_3 (.in(adder_2_cout));
  Adder adder_3 (.a(A), .b(not_1_out), .out(out_6), .cin(in_1), .cout(adder_3_cout));
  LED led_4 (.in(adder_3_cout));
  Adder adder_4 (.a(A), .b(negator_2_out), .out(out_7), .cin(in_1), .cout(adder_4_cout));
  LED led_5 (.in(adder_4_cout));
  Comparator comparator_1 (.a(out_4), .b({8{1'b0}}), .eq(comparator_1_eq));  // open: gt, lt
  LED led_6 (.in(comparator_1_eq));
  Comparator comparator_2 (.a(out_5), .b({8{1'b0}}), .eq(comparator_2_eq));  // open: gt, lt
  LED led_7 (.in(comparator_2_eq));
  Comparator comparator_3 (.a(out_6), .b({8{1'b0}}), .eq(comparator_3_eq));  // open: gt, lt
  LED led_8 (.in(comparator_3_eq));
  Comparator comparator_4 (.a(out_7), .b({8{1'b0}}), .eq(comparator_4_eq));  // open: gt, lt
  LED led_9 (.in(comparator_4_eq));
endmodule

module AddSub (
  input  WCarry,
  input  [7:0] A,
  input  [7:0] B,
  input  Sub,
  input  CarryBit,
  output [7:0] out_6
);

  wire adder_1_cout, comparator_1_eq, multiplexer_1_out, xor_1_out;
  wire [7:0] multiplexer_2_out, not_1_out;

  assign not_1_out = ~B;  // NOT_Gate not_1, 8 bits wide
  xor xor_1 (xor_1_out, Sub, CarryBit);
  Multiplexer multiplexer_1 (.in0(Sub), .in1(xor_1_out), .out(multiplexer_1_out), .sel(WCarry));
  Adder adder_1 (.a(A), .b(multiplexer_2_out), .out(out_6), .cin(multiplexer_1_out), .cout(adder_1_cout));
  Multiplexer #(.width(8)) multiplexer_2 (.in0(B), .in1(not_1_out), .out(multiplexer_2_out), .sel(Sub));
  LED led_1 (.in(adder_1_cout));
  Comparator comparator_1 (.a(out_6), .b({8{1'b0}}), .eq(comparator_1_eq));  // open: gt, lt
  LED led_2 (.in(comparator_1_eq));
endmodule

module CarryIn (
  input  Sub,
  input  CarryBit,
  input  WCarry,
  output Carry
);

  wire xor_1_out;

  xor xor_1 (xor_1_out, Sub, CarryBit);
  Multiplexer multiplexer_1 (.in0(Sub), .in1(xor_1_out), .out(Carry), .sel(WCarry));
endmodule
