// Logisim project bit32.2.circ as structural Verilog: 2 circuits, main circuit main
module main (
);

  wire ALU, and_2_out, and_3_out, and_4_out, and_6_out, and_7_out, and_8_out, and_9_out, and_10_out,
       and_11_out, and_12_out, and_13_out, and_14_out, and_15_out, and_16_out, and_17_out, and_18_out,
       and_19_out, and_20_out, and_21_out, and_22_out, and_23_out, and_24_out, and_25_out, and_26_out,
       and_27_out, and_28_out, and_29_out, and_30_out, and_31_out, and_32_out, and_33_out, and_34_out,
       and_36_out, and_37_out, and_38_out, button_1_out, button_2_out, button_3_out, Clk, clock_1_out, Cmp,
       comparator_1_eq, comparator_2_eq, comparator_3_eq, controlled_buffer_8_out, demultiplexer_1_out0,
       demultiplexer_1_out1, demultiplexer_2_out0, demultiplexer_2_out1, demultiplexer_2_out2,
       demultiplexer_2_out3, demultiplexer_2_out4, demultiplexer_2_out5, demultiplexer_2_out6,
       demultiplexer_2_out7, demultiplexer_2_out8, demultiplexer_2_out9, demultiplexer_2_out10,
       demultiplexer_2_out11, demultiplexer_2_out12, demultiplexer_2_out13, demultiplexer_2_out14,
       demultiplexer_2_out15, Exec, F, H, Int, j_k_ff_1_q, j_k_ff_1_qn, Jump, Latch, Load, not_1_out,
       not_2_out, not_3_out, not_4_out, not_5_out, or_1_out, or_4_out, or_6_out, or_7_out, or_9_out,
       or_11_out, ram_1_p2, Reset, RW, Stack, undriven_9, undriven_10, Word, xnor_1_out, xnor_2_out,
       xor_1_out, xor_2_out;
  wire [3:0] Cond, CVNZ, multiplexer_16_out;
  wire [4:0] multiplexer_12_out;
  wire [6:0] keyboard_1_data;
  wire [6:2] pla_1_out;
  wire [7:0] controlled_buffer_5_out, register_3_q, register_4_q, register_7_q, register_8_q, register_11_q,
       register_12_q, register_15_q, register_16_q, register_19_q, register_20_q, register_23_q,
       register_24_q, undriven, undriven_2, undriven_3, undriven_4, undriven_5, undriven_6;
  wire [15:0] A_q, B_q, C_q, controlled_buffer_6_out, D_q, E_q, F_q, G_q, H_q, I_q, J_q, K_q, L_q,
       register_2_q, register_6_q, register_10_q, register_14_q, register_18_q, register_22_q;
  wire [23:0] Code24;
  wire [26:0] multiplexer_12_out_2;
  wire [26:24] IR_q;
  wire [31:0] adder_1_out, adder_2_out, adder_3_out, Addr, and_35_out, Base, bit_extender_1_out,
       bit_extender_3_out, bit_extender_4_out, Const8, Data, Din, divider_1_out, divider_1_rem, Dout, fp_q,
       fpadder_1_out, fpdivider_1_out, fpmultiplier_1_out, fpnegator_1_p2, fpsubtractor_1_out, fptoint_1_p2,
       inttofp_1_p2, lr_q, multiplexer_1_out, multiplexer_4_out, multiplexer_6_out, multiplexer_7_out,
       multiplexer_11_out, multiplexer_14_out, multiplexer_15_out, multiplier_1_out, myadder_1_add,
       negator_1_out, not_6_out, Offset, Offset8, Offset24, or_10_out, PC, Primary, shifter_1_out,
       shifter_2_out, shifter_3_out, shifter_4_out, shifter_5_out, SP, SP_q, undriven_7, xor_3_out;
  wire [31:8] undriven_8;

  not not_1 (not_1_out, Addr[31]);
  Demultiplexer #(.select(2)) demultiplexer_1 (
    .out0(demultiplexer_1_out0), .out1(demultiplexer_1_out1), .in(Addr[31]), .sel(Addr[1:0]));  // open: out2, out3
  Multiplexer #(.width(32)) multiplexer_1 (.in0(Offset), .in1(Offset8), .out(multiplexer_1_out), .sel(Code24[21]));
  Multiplexer #(.select(4)) multiplexer_2 (
    .in0(1'b0), .in1(CVNZ[0]), .in2(not_2_out), .in3(CVNZ[1]), .in4(not_3_out), .in5(CVNZ[2]),
    .in6(not_4_out), .in7(CVNZ[3]), .in8(not_5_out), .in9(and_8_out), .in10(or_6_out), .in11(xor_1_out),
    .in12(xnor_1_out), .in13(or_7_out), .in14(and_10_out), .in15(1'b1), .out(Exec), .sel(Cond));
  Button button_1 (.out(button_1_out));
  // RAM #(.addrWidth(24), .clearpin("true"), .enables("line"), .line("quad"), .misaligned("true"), .trigger("falling")) ram_1: pin names not known; wires that end beside it: Addr[23:0], ram_1_p2, H, Code24[23], Clk, Dout[7:0], Dout[15:8], Dout[23:16], Dout[31:24], button_1_out
  and and_1 (ram_1_p2, not_1_out, RW);
  TTY #(.trigger("falling")) tty_1 (.data(Dout[6:0]), .clk(Clk), .we(demultiplexer_1_out0), .clr(Reset));
  Adder #(.width(32)) adder_1 (.a(Base), .b(multiplexer_1_out), .out(adder_1_out));  // open: cin, cout
  assign Data = or_1_out ? Din : 32'bz;  // Controlled_Buffer controlled_buffer_1
  or or_1 (or_1_out, ~Clk, or_4_out);  // OR_Gate
  or or_2 (Latch, or_4_out, and_2_out);
  and and_2 (and_2_out, ALU, ~Cmp);  // AND_Gate
  not not_2 (not_2_out, CVNZ[0]);
  not not_3 (not_3_out, CVNZ[1]);
  not not_4 (not_4_out, CVNZ[2]);
  or or_3 (Reset, button_1_out, button_2_out);
  Button button_2 (.out(button_2_out));
  and and_3 (and_3_out, Clk, demultiplexer_1_out1);
  Keyboard #(.trigger("falling")) keyboard_1 (
    .clk(and_3_out), .re(demultiplexer_1_out1), .clr(Reset), .data(keyboard_1_data));  // open: avail
  Multiplexer #(.width(32)) multiplexer_3 (.in0(PC), .in1(multiplexer_4_out), .out(Addr), .sel(and_4_out));
  Multiplexer #(.width(32)) multiplexer_4 (.in0(adder_1_out), .in1(SP), .out(multiplexer_4_out), .sel(Stack));
  and and_4 (and_4_out, Clk, j_k_ff_1_qn, Load);
  and and_5 (RW, Clk, Load, Code24[20]);
  assign Dout = RW ? Primary : 32'bz;  // Controlled_Buffer controlled_buffer_2
  and and_6 (and_6_out, Load, ~Code24[20]);  // AND_Gate
  or or_4 (or_4_out, and_6_out, and_7_out);
  and and_7 (and_7_out, Word, j_k_ff_1_q);
  not not_5 (not_5_out, CVNZ[3]);
  and and_8 (and_8_out, ~CVNZ[0], CVNZ[3]);  // AND_Gate
  or or_5 (Clk, clock_1_out, button_3_out);
  Clock clock_1 (.out(clock_1_out));
  Button button_3 (.out(button_3_out));
  assign bit_extender_1_out = {{25{1'b0}}, keyboard_1_data};  // Bit_Extender bit_extender_1
  J_K_Flip_Flop #(.trigger("falling")) j_k_ff_1 (
    .J(Word), .K(Word), .clk(Clk), .Q(j_k_ff_1_q), .Qn(j_k_ff_1_qn), .reset(Reset));  // open: preset
  or or_6 (or_6_out, CVNZ[0], ~CVNZ[3]);  // OR_Gate
  xor xor_1 (xor_1_out, CVNZ[1], CVNZ[2]);
  and and_9 (and_9_out, ~RW, not_1_out);  // AND_Gate
  assign Din = and_9_out ? {undriven_4, undriven_3, undriven_2, undriven} : 32'bz;  // Controlled_Buffer controlled_buffer_3
  assign Din = demultiplexer_1_out1 ? bit_extender_1_out : 32'bz;  // Controlled_Buffer controlled_buffer_4
  Register #(.width(32)) IR (.D(Data), .en(j_k_ff_1_qn), .clk(Clk), .Q({Cond, F, IR_q, Code24}), .clr(Reset));
  xor xor_2 (xor_2_out, CVNZ[1], CVNZ[2]);
  xnor xnor_1 (xnor_1_out, CVNZ[1], CVNZ[2]);
  or or_7 (or_7_out, CVNZ[0], xor_2_out);
  PLA #(.in_width(4), .out_width(8), .\table ("0xxx 00000000\n1000 00000001\n1001 00000010\n1010 00000000\n1011 00001000\n1100 00010000\n1101 00110000\n1110 00000000\n1111 11000000")) pla_1 (
    .in({Exec, IR_q}), .out({Word, pla_1_out[6], Stack, Load, Int, pla_1_out[2], ALU, Jump}));
  xnor xnor_2 (xnor_2_out, CVNZ[1], CVNZ[2]);
  and and_10 (and_10_out, ~CVNZ[0], xnor_2_out);  // AND_Gate
  Demultiplexer #(.select(4)) demultiplexer_2 (
    .out0(demultiplexer_2_out0), .out1(demultiplexer_2_out1), .out2(demultiplexer_2_out2),
    .out3(demultiplexer_2_out3), .out4(demultiplexer_2_out4), .out5(demultiplexer_2_out5),
    .out6(demultiplexer_2_out6), .out7(demultiplexer_2_out7), .out8(demultiplexer_2_out8),
    .out9(demultiplexer_2_out9), .out10(demultiplexer_2_out10), .out11(demultiplexer_2_out11),
    .out12(demultiplexer_2_out12), .out13(demultiplexer_2_out13), .out14(demultiplexer_2_out14),
    .out15(demultiplexer_2_out15), .in(Latch), .sel(Code24[3:0]));
  assign Offset24 = {{8{Code24[23]}}, Code24};  // Bit_Extender bit_extender_2
  Bit_Extender #(.out_width(32), .\type ("zero")) bit_extender_3 (.out(bit_extender_3_out));  // open: in
  assign bit_extender_4_out = {{16{1'b0}}, {undriven_6, undriven_5}};  // Bit_Extender bit_extender_4
  and and_11 (and_11_out, Code24[23], demultiplexer_2_out0);
  and and_12 (and_12_out, H, demultiplexer_2_out0);
  and and_13 (and_13_out, Code24[23], demultiplexer_2_out1);
  and and_14 (and_14_out, H, demultiplexer_2_out1);
  or or_8 (H, Code24[23], Code24[22]);
  assign Const8 = {{24{1'b0}}, Code24[15:8]};  // Bit_Extender bit_extender_5
  assign Offset8 = {{24{Code24[15]}}, Code24[15:8]};  // Bit_Extender bit_extender_6
  Multiplexer #(.select(2), .width(32)) multiplexer_5 (
    .in0(bit_extender_3_out), .in1(bit_extender_4_out), .in2(undriven_7), .in3(undriven_7),
    .sel({Code24[23], H}));  // open: out
  Register #(.trigger("falling"), .width(16)) A (.D(Data[31:16]), .en(and_11_out), .clk(Clk), .Q(A_q), .clr(Reset));
  Register #(.trigger("falling")) register_1 (
    .D(Data[15:8]), .en(and_12_out), .clk(Clk), .Q(register_2_q[15:8]), .clr(Reset));
  Register #(.trigger("falling")) register_2 (
    .D(Data[7:0]), .en(demultiplexer_2_out0), .clk(Clk), .Q(register_2_q[7:0]), .clr(Reset));
  Register #(.trigger("falling"), .width(16)) B (.D(Data[31:16]), .en(and_13_out), .clk(Clk), .Q(B_q), .clr(Reset));
  Register #(.trigger("falling")) register_3 (
    .D(Data[15:8]), .en(and_14_out), .clk(Clk), .Q(register_3_q), .clr(Reset));
  Register #(.trigger("falling")) register_4 (
    .D(Data[7:0]), .en(demultiplexer_2_out1), .clk(Clk), .Q(register_4_q), .clr(Reset));
  and and_15 (and_15_out, Code24[23], demultiplexer_2_out2);
  and and_16 (and_16_out, H, demultiplexer_2_out2);
  and and_17 (and_17_out, Code24[23], demultiplexer_2_out3);
  and and_18 (and_18_out, H, demultiplexer_2_out3);
  Register #(.trigger("falling"), .width(16)) C (.D(Data[31:16]), .en(and_15_out), .clk(Clk), .Q(C_q), .clr(Reset));
  Register #(.trigger("falling")) register_5 (
    .D(Data[15:8]), .en(and_16_out), .clk(Clk), .Q(register_6_q[15:8]), .clr(Reset));
  Register #(.trigger("falling")) register_6 (
    .D(Data[7:0]), .en(demultiplexer_2_out2), .clk(Clk), .Q(register_6_q[7:0]), .clr(Reset));
  Register #(.trigger("falling"), .width(16)) D (.D(Data[31:16]), .en(and_17_out), .clk(Clk), .Q(D_q), .clr(Reset));
  Register #(.trigger("falling")) register_7 (
    .D(Data[15:8]), .en(and_18_out), .clk(Clk), .Q(register_7_q), .clr(Reset));
  Register #(.trigger("falling")) register_8 (
    .D(Data[7:0]), .en(demultiplexer_2_out3), .clk(Clk), .Q(register_8_q), .clr(Reset));
  and and_19 (and_19_out, Code24[23], demultiplexer_2_out4);
  and and_20 (and_20_out, H, demultiplexer_2_out4);
  and and_21 (and_21_out, Code24[23], demultiplexer_2_out5);
  and and_22 (and_22_out, H, demultiplexer_2_out5);
  Register #(.trigger("falling"), .width(16)) E (.D(Data[31:16]), .en(and_19_out), .clk(Clk), .Q(E_q), .clr(Reset));
  Register #(.trigger("falling")) register_9 (
    .D(Data[15:8]), .en(and_20_out), .clk(Clk), .Q(register_10_q[15:8]), .clr(Reset));
  Register #(.trigger("falling")) register_10 (
    .D(Data[7:0]), .en(demultiplexer_2_out4), .clk(Clk), .Q(register_10_q[7:0]), .clr(Reset));
  Register #(.trigger("falling"), .width(16)) u_F (.D(Data[31:16]), .en(and_21_out), .clk(Clk), .Q(F_q), .clr(Reset));
  Register #(.trigger("falling")) register_11 (
    .D(Data[15:8]), .en(and_22_out), .clk(Clk), .Q(register_11_q), .clr(Reset));
  Register #(.trigger("falling")) register_12 (
    .D(Data[7:0]), .en(demultiplexer_2_out5), .clk(Clk), .Q(register_12_q), .clr(Reset));
  and and_23 (and_23_out, Code24[23], demultiplexer_2_out6);
  and and_24 (and_24_out, H, demultiplexer_2_out6);
  and and_25 (and_25_out, Code24[23], demultiplexer_2_out7);
  and and_26 (and_26_out, H, demultiplexer_2_out7);
  Register #(.trigger("falling"), .width(16)) G (.D(Data[31:16]), .en(and_23_out), .clk(Clk), .Q(G_q), .clr(Reset));
  Register #(.trigger("falling")) register_13 (
    .D(Data[15:8]), .en(and_24_out), .clk(Clk), .Q(register_14_q[15:8]), .clr(Reset));
  Register #(.trigger("falling")) register_14 (
    .D(Data[7:0]), .en(demultiplexer_2_out6), .clk(Clk), .Q(register_14_q[7:0]), .clr(Reset));
  Register #(.trigger("falling"), .width(16)) u_H (.D(Data[31:16]), .en(and_25_out), .clk(Clk), .Q(H_q), .clr(Reset));
  Register #(.trigger("falling")) register_15 (
    .D(Data[15:8]), .en(and_26_out), .clk(Clk), .Q(register_15_q), .clr(Reset));
  Register #(.trigger("falling")) register_16 (
    .D(Data[7:0]), .en(demultiplexer_2_out7), .clk(Clk), .Q(register_16_q), .clr(Reset));
  and and_27 (and_27_out, Code24[23], demultiplexer_2_out8);
  and and_28 (and_28_out, H, demultiplexer_2_out8);
  and and_29 (and_29_out, Code24[23], demultiplexer_2_out9);
  and and_30 (and_30_out, H, demultiplexer_2_out9);
  Register #(.trigger("falling"), .width(16)) I (.D(Data[31:16]), .en(and_27_out), .clk(H), .Q(I_q), .clr(Code24[23]));
  Register #(.trigger("falling")) register_17 (
    .D(Data[15:8]), .en(and_28_out), .clk(H), .Q(register_18_q[15:8]), .clr(Code24[23]));
  Register #(.trigger("falling")) register_18 (
    .D(Data[7:0]), .en(demultiplexer_2_out8), .clk(H), .Q(register_18_q[7:0]), .clr(Code24[23]));
  Register #(.trigger("falling"), .width(16)) J (.D(Data[31:16]), .en(and_29_out), .clk(H), .Q(J_q), .clr(Code24[23]));
  Register #(.trigger("falling")) register_19 (
    .D(Data[15:8]), .en(and_30_out), .clk(H), .Q(register_19_q), .clr(Code24[23]));
  Register #(.trigger("falling")) register_20 (
    .D(Data[7:0]), .en(demultiplexer_2_out9), .clk(H), .Q(register_20_q), .clr(Code24[23]));
  Register #(.trigger("falling"), .width(16)) K (.D(Data[31:16]), .en(and_31_out), .clk(Clk), .Q(K_q), .clr(Reset));
  and and_31 (and_31_out, Code24[23], demultiplexer_2_out10);
  and and_32 (and_32_out, H, demultiplexer_2_out10);
  Register #(.trigger("falling"), .width(16)) L (.D(Data[31:16]), .en(and_33_out), .clk(Clk), .Q(L_q), .clr(Reset));
  and and_33 (and_33_out, Code24[23], demultiplexer_2_out11);
  and and_34 (and_34_out, H, demultiplexer_2_out11);
  assign controlled_buffer_5_out = undriven_9 ? undriven_8[15:8] : 8'bz;  // Controlled_Buffer controlled_buffer_5
  assign controlled_buffer_6_out = undriven_10 ? undriven_8[31:16] : 16'bz;  // Controlled_Buffer controlled_buffer_6
  Register #(.trigger("falling")) register_21 (
    .D(Data[15:8]), .en(and_32_out), .clk(Clk), .Q(register_22_q[15:8]), .clr(Reset));
  Register #(.trigger("falling")) register_22 (
    .D(Data[7:0]), .en(demultiplexer_2_out10), .clk(Clk), .Q(register_22_q[7:0]), .clr(Reset));
  Register #(.trigger("falling")) register_23 (
    .D(Data[15:8]), .en(and_34_out), .clk(Clk), .Q(register_23_q), .clr(Reset));
  Register #(.trigger("falling")) register_24 (
    .D(Data[7:0]), .en(demultiplexer_2_out11), .clk(Clk), .Q(register_24_q), .clr(Reset));
  Multiplexer #(.width(32)) multiplexer_6 (
    .in0(adder_2_out), .in1(Data), .out(multiplexer_6_out), .sel(demultiplexer_2_out14));
  or or_9 (or_9_out, demultiplexer_2_out14, Stack);
  Multiplexer #(.width(32)) multiplexer_7 (
    .in0(adder_3_out), .in1(Data), .out(multiplexer_7_out), .sel(demultiplexer_2_out15));
  Register #(.trigger("falling"), .width(32)) lr (
    .D(Data), .en(demultiplexer_2_out12), .clk(Clk), .Q(lr_q), .clr(Reset));
  Register #(.trigger("falling"), .width(32)) fp (
    .D(Data), .en(demultiplexer_2_out13), .clk(Clk), .Q(fp_q), .clr(Reset));
  Register #(.trigger("falling"), .width(32)) u_SP (
    .D(multiplexer_6_out), .en(or_9_out), .clk(Clk), .Q(SP_q), .clr(Reset));
  Register #(.trigger("falling"), .width(32)) u_PC (.D(multiplexer_7_out), .en(1'b1), .clk(Clk), .Q(PC), .clr(Reset));
  Multiplexer #(.select(4), .width(32)) multiplexer_8 (
    .in0({A_q, register_2_q}), .in1({B_q, register_3_q, register_4_q}), .in2({C_q, register_6_q}),
    .in3({D_q, register_7_q, register_8_q}), .in4({E_q, register_10_q}),
    .in5({F_q, register_11_q, register_12_q}), .in6({G_q, register_14_q}),
    .in7({H_q, register_15_q, register_16_q}), .in8({I_q, register_18_q}),
    .in9({J_q, register_19_q, register_20_q}), .in10({K_q, register_22_q}),
    .in11({L_q, register_23_q, register_24_q}), .in12(lr_q), .in13(fp_q), .in14(SP_q), .in15(PC),
    .out(Primary), .sel(Code24[3:0]));
  Multiplexer #(.select(4), .width(32)) multiplexer_9 (
    .in0({A_q, register_2_q}), .in1({B_q, register_3_q, register_4_q}), .in2({C_q, register_6_q}),
    .in3({D_q, register_7_q, register_8_q}), .in4({E_q, register_10_q}),
    .in5({F_q, register_11_q, register_12_q}), .in6({G_q, register_14_q}),
    .in7({H_q, register_15_q, register_16_q}), .in8({I_q, register_18_q}),
    .in9({J_q, register_19_q, register_20_q}), .in10({K_q, register_22_q}),
    .in11({L_q, register_23_q, register_24_q}), .in12(lr_q), .in13(fp_q), .in14(SP_q), .in15(PC), .out(Base),
    .sel(Code24[7:4]));
  Multiplexer #(.select(4), .width(32)) multiplexer_10 (
    .in0({A_q, register_2_q}), .in1({B_q, register_3_q, register_4_q}), .in2({C_q, register_6_q}),
    .in3({D_q, register_7_q, register_8_q}), .in4({E_q, register_10_q}),
    .in5({F_q, register_11_q, register_12_q}), .in6({G_q, register_14_q}),
    .in7({H_q, register_15_q, register_16_q}), .in8({I_q, register_18_q}),
    .in9({J_q, register_19_q, register_20_q}), .in10({K_q, register_22_q}),
    .in11({L_q, register_23_q, register_24_q}), .in12(lr_q), .in13(fp_q), .in14(SP_q), .in15(PC),
    .out(Offset), .sel(Code24[11:8]));
  Adder #(.width(32)) adder_2 (.a(SP_q), .b(Offset8), .out(adder_2_out));  // open: cin, cout
  Multiplexer #(.width(32)) multiplexer_11 (.in0(32'h4), .in1(Offset24), .out(multiplexer_11_out), .sel(Jump));
  Multiplexer #(.width(32)) multiplexer_12 (
    .in0(Offset), .in1(Const8), .out({multiplexer_12_out_2, multiplexer_12_out}), .sel(Code24[21]));
  Multiplexer #(.width(32)) multiplexer_13 (.in0(SP_q), .in1(adder_2_out), .out(SP), .sel(Code24[20]));
  Adder #(.width(32)) adder_3 (.a(PC), .b(multiplexer_11_out), .out(adder_3_out));  // open: cin, cout
  Negator #(.width(32)) negator_1 (.in({multiplexer_12_out_2, multiplexer_12_out}), .out(negator_1_out));
  assign not_6_out = ~{multiplexer_12_out_2, multiplexer_12_out};  // NOT_Gate not_6, 32 bits wide
  assign and_35_out = Base & {multiplexer_12_out_2, multiplexer_12_out};  // AND_Gate and_35, 32 bits wide
  assign or_10_out = Base | {multiplexer_12_out_2, multiplexer_12_out};  // OR_Gate or_10, 32 bits wide
  assign xor_3_out = Base ^ {multiplexer_12_out_2, multiplexer_12_out};  // XOR_Gate xor_3, 32 bits wide
  // IntToFP #(.width(32)) inttofp_1: pin names not known; wires that end beside it: {multiplexer_12_out_2, multiplexer_12_out}, inttofp_1_p2
  FPAdder fpadder_1 (.a(Base), .b({multiplexer_12_out_2, multiplexer_12_out}), .out(fpadder_1_out));
  FPSubtractor fpsubtractor_1 (.a(Base), .b({multiplexer_12_out_2, multiplexer_12_out}), .out(fpsubtractor_1_out));
  // FPToInt #(.width(32)) fptoint_1: pin names not known; wires that end beside it: {multiplexer_12_out_2, multiplexer_12_out}, fptoint_1_p2
  // FPNegator fpnegator_1: pin names not known; wires that end beside it: {multiplexer_12_out_2, multiplexer_12_out}, fpnegator_1_p2
  FPMultiplier fpmultiplier_1 (.a(Base), .b({multiplexer_12_out_2, multiplexer_12_out}), .out(fpmultiplier_1_out));
  FPDivider fpdivider_1 (.a(Base), .b({multiplexer_12_out_2, multiplexer_12_out}), .out(fpdivider_1_out));
  Multiplier #(.width(32)) multiplier_1 (
    .a(Base), .b({multiplexer_12_out_2, multiplexer_12_out}), .out(multiplier_1_out));  // open: cin, cout
  Divider #(.width(32)) divider_1 (
    .a(Base), .b({multiplexer_12_out_2, multiplexer_12_out}), .out(divider_1_out), .rem(divider_1_rem));  // open: upper
  Shifter #(.shift("lr"), .width(32)) shifter_1 (.in(Base), .\dist (multiplexer_12_out), .out(shifter_1_out));
  Shifter #(.width(32)) shifter_2 (.in(Base), .\dist (multiplexer_12_out), .out(shifter_2_out));
  Shifter #(.shift("ar"), .width(32)) shifter_3 (.in(Base), .\dist (multiplexer_12_out), .out(shifter_3_out));
  Shifter #(.shift("rl"), .width(32)) shifter_4 (.in(Base), .\dist (multiplexer_12_out), .out(shifter_4_out));
  Shifter #(.shift("rr"), .width(32)) shifter_5 (.in(Base), .\dist (multiplexer_12_out), .out(shifter_5_out));
  Multiplexer #(.width(32)) multiplexer_14 (
    .in0({multiplexer_12_out_2, multiplexer_12_out}), .in1(negator_1_out), .out(multiplexer_14_out),
    .sel(and_36_out));
  MyAdder myadder_1 (
    .A(Base), .B(multiplexer_14_out), .WH({Code24[23], H}), .Cin(controlled_buffer_8_out),
    .Cout(multiplexer_16_out[3]), .V(multiplexer_16_out[2]), .Add(myadder_1_add));
  and and_36 (and_36_out, ~Code24[20], ~Code24[19], Code24[18]);  // AND_Gate
  assign Data = and_37_out ? multiplexer_15_out : 32'bz;  // Controlled_Buffer controlled_buffer_7
  Multiplexer #(.select(5), .width(32)) multiplexer_15 (
    .in0({multiplexer_12_out_2, multiplexer_12_out}), .in1(myadder_1_add), .in2(myadder_1_add),
    .in3(myadder_1_add), .in4(negator_1_out), .in5(myadder_1_add), .in6(myadder_1_add), .in7(myadder_1_add),
    .in8(not_6_out), .in9(negator_1_out), .in10(and_35_out), .in11(and_35_out), .in13(or_10_out),
    .in14(xor_3_out), .in15(xor_3_out), .in16(inttofp_1_p2), .in17(fpadder_1_out), .in18(fpsubtractor_1_out),
    .in19(fpsubtractor_1_out), .in20(fptoint_1_p2), .in21(fpnegator_1_p2), .in22(fpmultiplier_1_out),
    .in23(fpdivider_1_out), .in24(multiplier_1_out), .in25(divider_1_out), .in26(divider_1_rem),
    .in27(shifter_1_out), .in28(shifter_2_out), .in29(shifter_3_out), .in30(shifter_4_out),
    .in31(shifter_5_out), .out(multiplexer_15_out), .sel(Code24[20:16]));  // open: in12
  and and_37 (and_37_out, Clk, ALU);
  and and_38 (and_38_out, ~Code24[20], ~Code24[19], Code24[17], ~Code24[16]);  // AND_Gate
  and and_39 (Cmp, ALU, ~Code24[20], Code24[16], Code24[17]);  // AND_Gate
  Comparator comparator_1 (.a(Data[7:0]), .b({8{1'b0}}), .eq(comparator_1_eq));  // open: gt, lt
  Comparator #(.width(16)) comparator_2 (.a(Data[15:0]), .b({16{1'b0}}), .eq(comparator_2_eq));  // open: gt, lt
  Comparator #(.width(32)) comparator_3 (.a(Data), .b({32{1'b0}}), .eq(comparator_3_eq));  // open: gt, lt
  Multiplexer #(.select(2)) multiplexer_16 (
    .in0(comparator_1_eq), .in1(comparator_2_eq), .in2(comparator_3_eq), .in3(comparator_3_eq),
    .out(multiplexer_16_out[0]), .sel({Code24[23], H}));
  Multiplexer #(.select(2)) multiplexer_17 (
    .in0(Data[7]), .in1(Data[15]), .in2(Data[31]), .in3(Data[31]), .out(multiplexer_16_out[1]),
    .sel({Code24[23], H}));
  Register #(.trigger("falling"), .width(4)) register_25 (
    .D(multiplexer_16_out), .en(or_11_out), .clk(Clk), .Q(CVNZ), .clr(Reset));
  or or_11 (or_11_out, Cmp, F);
  assign controlled_buffer_8_out = and_38_out ? CVNZ[3] : 1'bz;  // Controlled_Buffer controlled_buffer_8

  // Other names for the same wires on the sheet: Rd[3:0] = Code24[3:0]; Rs[3:0] = Code24[7:4]; I = Code24[21];
  //   Rs2[3:0] = Code24[11:8]; W = Code24[23]; Op5[4:0] = Code24[20:16]; D = Code24[20]
endmodule

module MyAdder (
  input  [31:0] A,
  input  [31:0] B,
  input  Cin,
  input  [1:0] WH,
  output [31:0] Add,
  output V,
  output Cout
);

  wire adder_1_cout, adder_2_cout, adder_3_cout, adder_4_cout, adder_5_cout, adder_6_cout, xor_1_out,
       xor_2_out, xor_3_out;

  Adder #(.width(7)) adder_1 (.a(A[6:0]), .b(B[6:0]), .out(Add[6:0]), .cin(Cin), .cout(adder_1_cout));
  Adder #(.width(1)) adder_2 (.a(A[7]), .b(B[7]), .out(Add[7]), .cin(adder_1_cout), .cout(adder_2_cout));
  Adder #(.width(7)) adder_3 (.a(A[14:8]), .b(B[14:8]), .out(Add[14:8]), .cin(adder_2_cout), .cout(adder_3_cout));
  Adder #(.width(1)) adder_4 (.a(A[15]), .b(B[15]), .out(Add[15]), .cin(adder_3_cout), .cout(adder_4_cout));
  Adder #(.width(15)) adder_5 (.a(A[30:16]), .b(B[30:16]), .out(Add[30:16]), .cin(adder_4_cout), .cout(adder_5_cout));
  Adder #(.width(1)) adder_6 (.a(A[31]), .b(B[31]), .out(Add[31]), .cin(adder_5_cout), .cout(adder_6_cout));
  xor xor_1 (xor_1_out, adder_6_cout, adder_5_cout);
  Multiplexer #(.select(2)) multiplexer_1 (
    .in0(adder_2_cout), .in1(adder_4_cout), .in2(adder_6_cout), .in3(adder_6_cout), .out(Cout), .sel(WH));
  xor xor_2 (xor_2_out, adder_2_cout, adder_1_cout);
  xor xor_3 (xor_3_out, adder_4_cout, adder_3_cout);
  Multiplexer #(.select(2)) multiplexer_2 (
    .in0(xor_2_out), .in1(xor_3_out), .in2(xor_1_out), .in3(xor_1_out), .out(V), .sel(WH));
endmodule
