// Logisim project bit32.3.circ as structural Verilog: 2 circuits, main circuit main
module main (
);

  wire ALU, and_1_out, and_2_out, and_4_out, and_5_out, and_6_out, and_7_out, and_8_out, and_10_out,
       and_11_out, and_13_out, and_14_out, and_16_out, button_1_out, button_2_out, button_3_out, Clk,
       clock_1_out, Cmp, comparator_1_eq, comparator_2_eq, comparator_3_eq, controlled_buffer_6_out,
       demultiplexer_1_out0, demultiplexer_1_out1, demultiplexer_2_out0, demultiplexer_2_out1,
       demultiplexer_2_out2, demultiplexer_2_out3, demultiplexer_2_out4, demultiplexer_2_out5,
       demultiplexer_2_out6, demultiplexer_2_out7, demultiplexer_2_out8, demultiplexer_2_out9,
       demultiplexer_2_out10, demultiplexer_2_out11, demultiplexer_2_out12, demultiplexer_2_out13,
       demultiplexer_2_out14, demultiplexer_2_out15, Exec, F, Int, j_k_ff_1_q, j_k_ff_1_qn, Jump, Latch,
       Load, multiplexer_17_out, multiplexer_18_out, not_1_out, not_2_out, not_3_out, not_4_out, or_1_out,
       or_2_out, or_3_out, or_4_out, or_7_out, or_9_out, or_10_out, or_12_out, ram_1_p2, Reset, RW, Stack,
       Word, xnor_1_out, xnor_2_out, xor_1_out, xor_2_out;
  wire [3:0] Cond, CVNZ, multiplexer_20_out;
  wire [4:0] multiplexer_14_out;
  wire [6:0] keyboard_1_data;
  wire [6:2] pla_1_out;
  wire [7:0] undriven, undriven_2, undriven_3, undriven_4;
  wire [23:0] Code24;
  wire [26:0] multiplexer_14_out_2;
  wire [26:24] IR_q;
  wire [31:0] A_q, adder_1_out, adder_2_out, adder_3_out, Addr, and_12_out, B_q, Base, bit_extender_1_out,
       bit_extender_2_out, bit_extender_3_out, C_q, Const8, D_q, Data, Din, divider_1_out, divider_1_rem,
       Dout, E_q, F_q, FP_q, fpadder_1_out, fpdivider_1_out, fpmultiplier_1_out, fpnegator_1_p2,
       fpsubtractor_1_out, fptoint_1_p2, G_q, H_q, I_q, inttofp_1_p2, J_q, K_q, L_q, LR_q, multiplexer_2_out,
       multiplexer_3_out, multiplexer_5_out, multiplexer_6_out, multiplexer_7_out, multiplexer_8_out,
       multiplexer_9_out, multiplexer_15_out, multiplexer_16_out, multiplier_1_out, myadder_1_add,
       negator_1_out, not_5_out, Offset, Offset8, Offset24, or_11_out, PC, Primary, shifter_1_out,
       shifter_2_out, shifter_3_out, shifter_4_out, shifter_5_out, SP, SP_q, xor_3_out;

  Multiplexer #(.select(4)) multiplexer_1 (
    .in0(1'b0), .in1(CVNZ[0]), .in2(not_1_out), .in3(CVNZ[1]), .in4(not_2_out), .in5(CVNZ[2]),
    .in6(not_3_out), .in7(or_1_out), .in8(and_1_out), .in9(and_2_out), .in10(or_3_out), .in11(xor_1_out),
    .in12(xnor_1_out), .in13(or_4_out), .in14(and_5_out), .in15(1'b1), .out(Exec), .sel(Cond));
  not not_1 (not_1_out, CVNZ[0]);
  not not_2 (not_2_out, CVNZ[1]);
  not not_3 (not_3_out, CVNZ[2]);
  or or_1 (or_1_out, CVNZ[0], CVNZ[3]);
  and and_1 (and_1_out, ~CVNZ[0], ~CVNZ[3]);  // AND_Gate
  and and_2 (and_2_out, ~CVNZ[0], CVNZ[3]);  // AND_Gate
  not not_4 (not_4_out, Addr[31]);
  or or_2 (or_2_out, Code24[22], Code24[23]);
  Demultiplexer #(.select(2)) demultiplexer_1 (
    .out0(demultiplexer_1_out0), .out1(demultiplexer_1_out1), .in(Addr[31]), .sel(Addr[1:0]));  // open: out2, out3
  or or_3 (or_3_out, CVNZ[0], ~CVNZ[3]);  // OR_Gate
  xor xor_1 (xor_1_out, CVNZ[1], CVNZ[2]);
  Button button_1 (.out(button_1_out));
  // RAM #(.addrWidth(24), .clearpin("true"), .enables("line"), .line("quad"), .misaligned("true"), .trigger("falling")) ram_1: pin names not known; wires that end beside it: Addr[23:0], ram_1_p2, or_2_out, Code24[23], Clk, Dout[7:0], Dout[15:8], Dout[23:16], Dout[31:24], button_1_out
  and and_3 (ram_1_p2, not_4_out, RW);
  TTY #(.trigger("falling")) tty_1 (.data(Dout[6:0]), .clk(Clk), .we(demultiplexer_1_out0), .clr(Reset));
  xor xor_2 (xor_2_out, CVNZ[1], CVNZ[2]);
  xnor xnor_1 (xnor_1_out, CVNZ[1], CVNZ[2]);
  or or_4 (or_4_out, CVNZ[0], xor_2_out);
  or or_5 (Reset, button_1_out, button_2_out);
  Button button_2 (.out(button_2_out));
  and and_4 (and_4_out, Clk, demultiplexer_1_out1);
  Keyboard #(.trigger("falling")) keyboard_1 (
    .clk(and_4_out), .re(demultiplexer_1_out1), .clr(Reset), .data(keyboard_1_data));  // open: avail
  xnor xnor_2 (xnor_2_out, CVNZ[1], CVNZ[2]);
  and and_5 (and_5_out, ~CVNZ[0], xnor_2_out);  // AND_Gate
  or or_6 (Clk, clock_1_out, button_3_out);
  Clock clock_1 (.out(clock_1_out));
  Button button_3 (.out(button_3_out));
  assign bit_extender_1_out = {{25{1'b0}}, keyboard_1_data};  // Bit_Extender bit_extender_1
  Multiplexer #(.width(32)) multiplexer_2 (.in0(Offset), .in1(Const8), .out(multiplexer_2_out), .sel(Code24[21]));
  assign Data = or_7_out ? Din : 32'bz;  // Controlled_Buffer controlled_buffer_1
  or or_7 (or_7_out, ~Clk, or_9_out);  // OR_Gate
  or or_8 (Latch, or_9_out, and_7_out);
  and and_6 (and_6_out, ~RW, not_4_out);  // AND_Gate
  assign Din = and_6_out ? {undriven_4, undriven_3, undriven_2, undriven} : 32'bz;  // Controlled_Buffer controlled_buffer_2
  assign Din = demultiplexer_1_out1 ? bit_extender_1_out : 32'bz;  // Controlled_Buffer controlled_buffer_3
  Adder #(.width(32)) adder_1 (.a(Base), .b(multiplexer_2_out), .out(adder_1_out));  // open: cin, cout
  Multiplexer #(.width(32)) multiplexer_3 (.in0(adder_1_out), .in1(SP), .out(multiplexer_3_out), .sel(Stack));
  assign Dout = RW ? Primary : 32'bz;  // Controlled_Buffer controlled_buffer_4
  or or_9 (or_9_out, and_10_out, and_11_out);
  and and_7 (and_7_out, ALU, ~Cmp);  // AND_Gate
  assign bit_extender_2_out = {{24{1'b0}}, Data[7:0]};  // Bit_Extender bit_extender_2
  assign bit_extender_3_out = {{16{1'b0}}, Data[15:0]};  // Bit_Extender bit_extender_3
  Multiplexer #(.width(32)) multiplexer_4 (.in0(PC), .in1(multiplexer_3_out), .out(Addr), .sel(and_8_out));
  and and_8 (and_8_out, Clk, j_k_ff_1_qn, Load);
  and and_9 (RW, Clk, Load, Code24[20]);
  and and_10 (and_10_out, Load, ~Code24[20]);  // AND_Gate
  and and_11 (and_11_out, Word, j_k_ff_1_q);
  J_K_Flip_Flop #(.trigger("falling")) j_k_ff_1 (
    .J(Word), .K(Word), .clk(Clk), .Q(j_k_ff_1_q), .Qn(j_k_ff_1_qn), .reset(Reset));  // open: preset
  Multiplexer #(.width(32)) multiplexer_5 (
    .in0(bit_extender_2_out), .in1(bit_extender_3_out), .out(multiplexer_5_out), .sel(Code24[22]));
  Multiplexer #(.width(32)) multiplexer_6 (
    .in0(multiplexer_5_out), .in1(Data), .out(multiplexer_6_out), .sel(Code24[23]));
  Demultiplexer #(.select(4)) demultiplexer_2 (
    .out0(demultiplexer_2_out0), .out1(demultiplexer_2_out1), .out2(demultiplexer_2_out2),
    .out3(demultiplexer_2_out3), .out4(demultiplexer_2_out4), .out5(demultiplexer_2_out5),
    .out6(demultiplexer_2_out6), .out7(demultiplexer_2_out7), .out8(demultiplexer_2_out8),
    .out9(demultiplexer_2_out9), .out10(demultiplexer_2_out10), .out11(demultiplexer_2_out11),
    .out12(demultiplexer_2_out12), .out13(demultiplexer_2_out13), .out14(demultiplexer_2_out14),
    .out15(demultiplexer_2_out15), .in(Latch), .sel(Code24[3:0]));
  Register #(.trigger("falling"), .width(32)) A (
    .D(multiplexer_6_out), .en(demultiplexer_2_out0), .clk(Clk), .Q(A_q), .clr(Reset));
  Register #(.trigger("falling"), .width(32)) B (
    .D(multiplexer_6_out), .en(demultiplexer_2_out1), .clk(Clk), .Q(B_q), .clr(Reset));
  Register #(.trigger("falling"), .width(32)) C (
    .D(multiplexer_6_out), .en(demultiplexer_2_out2), .clk(Clk), .Q(C_q), .clr(Reset));
  Register #(.trigger("falling"), .width(32)) D (
    .D(multiplexer_6_out), .en(demultiplexer_2_out3), .clk(Clk), .Q(D_q), .clr(Reset));
  Register #(.width(32)) IR (.D(Data), .en(j_k_ff_1_qn), .clk(Clk), .Q({Cond, F, IR_q, Code24}), .clr(Reset));
  PLA #(.in_width(4), .out_width(8), .\table ("0xxx 00000000\n1000 00000001\n1001 00000010\n1010 00000000\n1011 00001000\n1100 00010000\n1101 00110000\n1110 00000000\n1111 11000000")) pla_1 (
    .in({Exec, IR_q}), .out({Word, pla_1_out[6], Stack, Load, Int, pla_1_out[2], ALU, Jump}));
  Register #(.trigger("falling"), .width(32)) E (
    .D(multiplexer_6_out), .en(demultiplexer_2_out4), .clk(Clk), .Q(E_q), .clr(Reset));
  Register #(.trigger("falling"), .width(32)) u_F (
    .D(multiplexer_6_out), .en(demultiplexer_2_out5), .clk(Clk), .Q(F_q), .clr(Reset));
  Register #(.trigger("falling"), .width(32)) G (
    .D(multiplexer_6_out), .en(demultiplexer_2_out6), .clk(Clk), .Q(G_q), .clr(Reset));
  Register #(.trigger("falling"), .width(32)) H (
    .D(multiplexer_6_out), .en(demultiplexer_2_out7), .clk(Clk), .Q(H_q), .clr(Reset));
  assign Offset24 = {{8{Code24[23]}}, Code24};  // Bit_Extender bit_extender_4
  assign Const8 = {{24{1'b0}}, Code24[15:8]};  // Bit_Extender bit_extender_5
  assign Offset8 = {{24{Code24[15]}}, Code24[15:8]};  // Bit_Extender bit_extender_6
  Register #(.trigger("falling"), .width(32)) I (
    .D(multiplexer_6_out), .en(demultiplexer_2_out8), .clk(Clk), .Q(I_q), .clr(Reset));
  Register #(.trigger("falling"), .width(32)) J (
    .D(multiplexer_6_out), .en(demultiplexer_2_out9), .clk(Clk), .Q(J_q), .clr(Reset));
  Register #(.trigger("falling"), .width(32)) K (
    .D(multiplexer_6_out), .en(demultiplexer_2_out10), .clk(Clk), .Q(K_q), .clr(Reset));
  Register #(.trigger("falling"), .width(32)) L (
    .D(multiplexer_6_out), .en(demultiplexer_2_out11), .clk(Clk), .Q(L_q), .clr(Reset));
  Multiplexer #(.width(32)) multiplexer_7 (
    .in0(adder_2_out), .in1(multiplexer_6_out), .out(multiplexer_7_out), .sel(demultiplexer_2_out14));
  Register #(.trigger("falling"), .width(32)) LR (
    .D(multiplexer_6_out), .en(demultiplexer_2_out12), .clk(Clk), .Q(LR_q), .clr(Reset));
  Register #(.trigger("falling"), .width(32)) FP (
    .D(multiplexer_6_out), .en(demultiplexer_2_out13), .clk(Clk), .Q(FP_q), .clr(Reset));
  Register #(.trigger("falling"), .width(32)) u_SP (
    .D(multiplexer_7_out), .en(or_10_out), .clk(Clk), .Q(SP_q), .clr(Reset));
  or or_10 (or_10_out, demultiplexer_2_out14, Stack);
  Register #(.trigger("falling"), .width(32)) u_PC (.D(multiplexer_8_out), .en(1'b1), .clk(Clk), .Q(PC), .clr(Reset));
  Multiplexer #(.width(32)) multiplexer_8 (
    .in0(adder_3_out), .in1(multiplexer_6_out), .out(multiplexer_8_out), .sel(demultiplexer_2_out15));
  Adder #(.width(32)) adder_2 (.a(SP_q), .b(Offset8), .out(adder_2_out));  // open: cin, cout
  Multiplexer #(.width(32)) multiplexer_9 (.in0(32'h4), .in1(Offset24), .out(multiplexer_9_out), .sel(Jump));
  Multiplexer #(.width(32)) multiplexer_10 (.in0(SP_q), .in1(adder_2_out), .out(SP), .sel(Code24[20]));
  Adder #(.width(32)) adder_3 (.a(PC), .b(multiplexer_9_out), .out(adder_3_out));  // open: cin, cout
  Multiplexer #(.select(4), .width(32)) multiplexer_11 (
    .in0(A_q), .in1(B_q), .in2(C_q), .in3(D_q), .in4(E_q), .in5(F_q), .in6(G_q), .in7(H_q), .in8(I_q),
    .in9(J_q), .in10(K_q), .in11(L_q), .in12(LR_q), .in13(FP_q), .in14(SP_q), .in15(PC), .out(Primary),
    .sel(Code24[3:0]));
  Multiplexer #(.select(4), .width(32)) multiplexer_12 (
    .in0(A_q), .in1(B_q), .in2(C_q), .in3(D_q), .in4(E_q), .in5(F_q), .in6(G_q), .in7(H_q), .in8(I_q),
    .in9(J_q), .in10(K_q), .in11(L_q), .in12(LR_q), .in13(FP_q), .in14(SP_q), .in15(PC), .out(Base),
    .sel(Code24[7:4]));
  Multiplexer #(.select(4), .width(32)) multiplexer_13 (
    .in0(A_q), .in1(B_q), .in2(C_q), .in3(D_q), .in4(E_q), .in5(F_q), .in6(G_q), .in7(H_q), .in8(I_q),
    .in9(J_q), .in10(K_q), .in11(L_q), .in12(LR_q), .in13(FP_q), .in14(SP_q), .in15(PC), .out(Offset),
    .sel(Code24[11:8]));
  Multiplexer #(.width(32)) multiplexer_14 (
    .in0(Offset), .in1(Const8), .out({multiplexer_14_out_2, multiplexer_14_out}), .sel(Code24[21]));
  Negator #(.width(32)) negator_1 (.in({multiplexer_14_out_2, multiplexer_14_out}), .out(negator_1_out));
  assign not_5_out = ~{multiplexer_14_out_2, multiplexer_14_out};  // NOT_Gate not_5, 32 bits wide
  assign and_12_out = Base & {multiplexer_14_out_2, multiplexer_14_out};  // AND_Gate and_12, 32 bits wide
  assign or_11_out = Base | {multiplexer_14_out_2, multiplexer_14_out};  // OR_Gate or_11, 32 bits wide
  assign xor_3_out = Base ^ {multiplexer_14_out_2, multiplexer_14_out};  // XOR_Gate xor_3, 32 bits wide
  // IntToFP #(.width(32)) inttofp_1: pin names not known; wires that end beside it: {multiplexer_14_out_2, multiplexer_14_out}, inttofp_1_p2
  FPAdder fpadder_1 (.a(Base), .b({multiplexer_14_out_2, multiplexer_14_out}), .out(fpadder_1_out));
  FPSubtractor fpsubtractor_1 (.a(Base), .b({multiplexer_14_out_2, multiplexer_14_out}), .out(fpsubtractor_1_out));
  // FPToInt #(.width(32)) fptoint_1: pin names not known; wires that end beside it: {multiplexer_14_out_2, multiplexer_14_out}, fptoint_1_p2
  // FPNegator fpnegator_1: pin names not known; wires that end beside it: {multiplexer_14_out_2, multiplexer_14_out}, fpnegator_1_p2
  FPMultiplier fpmultiplier_1 (.a(Base), .b({multiplexer_14_out_2, multiplexer_14_out}), .out(fpmultiplier_1_out));
  FPDivider fpdivider_1 (.a(Base), .b({multiplexer_14_out_2, multiplexer_14_out}), .out(fpdivider_1_out));
  Multiplier #(.width(32)) multiplier_1 (
    .a(Base), .b({multiplexer_14_out_2, multiplexer_14_out}), .out(multiplier_1_out));  // open: cin, cout
  Divider #(.width(32)) divider_1 (
    .a(Base), .b({multiplexer_14_out_2, multiplexer_14_out}), .out(divider_1_out), .rem(divider_1_rem));  // open: upper
  Shifter #(.shift("lr"), .width(32)) shifter_1 (.in(Base), .\dist (multiplexer_14_out), .out(shifter_1_out));
  Shifter #(.width(32)) shifter_2 (.in(Base), .\dist (multiplexer_14_out), .out(shifter_2_out));
  Shifter #(.shift("ar"), .width(32)) shifter_3 (.in(Base), .\dist (multiplexer_14_out), .out(shifter_3_out));
  Shifter #(.shift("rl"), .width(32)) shifter_4 (.in(Base), .\dist (multiplexer_14_out), .out(shifter_4_out));
  Shifter #(.shift("rr"), .width(32)) shifter_5 (.in(Base), .\dist (multiplexer_14_out), .out(shifter_5_out));
  MyAdder myadder_1 (
    .H(Code24[22]), .W(Code24[23]), .A(Base), .B(multiplexer_15_out), .Cin(controlled_buffer_6_out),
    .Cout(multiplexer_20_out[3]), .Add(myadder_1_add), .V(multiplexer_20_out[2]));
  Multiplexer #(.width(32)) multiplexer_15 (
    .in0({multiplexer_14_out_2, multiplexer_14_out}), .in1(negator_1_out), .out(multiplexer_15_out),
    .sel(and_13_out));
  Multiplexer #(.select(5), .width(32)) multiplexer_16 (
    .in0({multiplexer_14_out_2, multiplexer_14_out}), .in1(myadder_1_add), .in2(myadder_1_add),
    .in3(myadder_1_add), .in4(negator_1_out), .in5(myadder_1_add), .in6(myadder_1_add), .in7(myadder_1_add),
    .in8(not_5_out), .in9(negator_1_out), .in10(and_12_out), .in11(and_12_out), .in13(or_11_out),
    .in14(xor_3_out), .in15(xor_3_out), .in16(inttofp_1_p2), .in17(fpadder_1_out), .in18(fpsubtractor_1_out),
    .in19(fpsubtractor_1_out), .in20(fptoint_1_p2), .in21(fpnegator_1_p2), .in22(fpmultiplier_1_out),
    .in23(fpdivider_1_out), .in24(multiplier_1_out), .in25(divider_1_out), .in26(divider_1_rem),
    .in27(shifter_1_out), .in28(shifter_2_out), .in29(shifter_3_out), .in30(shifter_4_out),
    .in31(shifter_5_out), .out(multiplexer_16_out), .sel(Code24[20:16]));  // open: in12
  and and_13 (and_13_out, ~Code24[20], ~Code24[19], Code24[18]);  // AND_Gate
  and and_14 (and_14_out, Clk, ALU);
  assign Data = and_14_out ? multiplexer_16_out : 32'bz;  // Controlled_Buffer controlled_buffer_5
  and and_15 (Cmp, ALU, ~Code24[20], Code24[16], Code24[17]);  // AND_Gate
  and and_16 (and_16_out, ~Code24[20], ~Code24[19], Code24[17], ~Code24[16]);  // AND_Gate
  Comparator comparator_1 (.a(Data[7:0]), .b({8{1'b0}}), .eq(comparator_1_eq));  // open: gt, lt
  Comparator #(.width(16)) comparator_2 (.a(Data[15:0]), .b({16{1'b0}}), .eq(comparator_2_eq));  // open: gt, lt
  Comparator #(.width(32)) comparator_3 (.a(Data), .b({32{1'b0}}), .eq(comparator_3_eq));  // open: gt, lt
  Multiplexer multiplexer_17 (.in0(comparator_1_eq), .in1(comparator_2_eq), .out(multiplexer_17_out), .sel(Code24[22]));
  Multiplexer multiplexer_18 (.in0(Data[7]), .in1(Data[15]), .out(multiplexer_18_out), .sel(Code24[22]));
  Multiplexer multiplexer_19 (.in0(multiplexer_18_out), .in1(Data[31]), .out(multiplexer_20_out[1]), .sel(Code24[23]));
  or or_12 (or_12_out, Cmp, F);
  Multiplexer multiplexer_20 (
    .in0(multiplexer_17_out), .in1(comparator_3_eq), .out(multiplexer_20_out[0]), .sel(Code24[23]));
  Register #(.trigger("falling"), .width(4)) register_1 (
    .D(multiplexer_20_out), .en(or_12_out), .clk(Clk), .Q(CVNZ), .clr(Reset));
  assign controlled_buffer_6_out = and_16_out ? CVNZ[3] : 1'bz;  // Controlled_Buffer controlled_buffer_6

  // Other names for the same wires on the sheet: Rd[3:0] = Code24[3:0]; Rs[3:0] = Code24[7:4]; I = Code24[21];
  //   H = Code24[22]; W = Code24[23]; Rs2[3:0] = Code24[11:8]; Op5[4:0] = Code24[20:16]; D = Code24[20]
endmodule

module MyAdder (
  input  [31:0] A,
  input  [31:0] B,
  input  Cin,
  input  H,
  input  W,
  output V,
  output Cout,
  output [31:0] Add
);

  wire adder_1_cout, adder_2_cout, adder_3_cout, adder_4_cout, adder_5_cout, adder_6_cout, multiplexer_1_out,
       multiplexer_3_out, xor_1_out, xor_2_out, xor_3_out;

  Multiplexer multiplexer_1 (.in0(adder_2_cout), .in1(adder_4_cout), .out(multiplexer_1_out), .sel(H));
  Multiplexer multiplexer_2 (.in0(multiplexer_1_out), .in1(adder_6_cout), .out(Cout), .sel(W));
  Adder #(.width(7)) adder_1 (.a(A[6:0]), .b(B[6:0]), .out(Add[6:0]), .cin(Cin), .cout(adder_1_cout));
  Adder #(.width(1)) adder_2 (.a(A[7]), .b(B[7]), .out(Add[7]), .cin(adder_1_cout), .cout(adder_2_cout));
  Adder #(.width(7)) adder_3 (.a(A[14:8]), .b(B[14:8]), .out(Add[14:8]), .cin(adder_2_cout), .cout(adder_3_cout));
  Adder #(.width(1)) adder_4 (.a(A[15]), .b(B[15]), .out(Add[15]), .cin(adder_3_cout), .cout(adder_4_cout));
  Adder #(.width(15)) adder_5 (.a(A[30:16]), .b(B[30:16]), .out(Add[30:16]), .cin(adder_4_cout), .cout(adder_5_cout));
  Adder #(.width(1)) adder_6 (.a(A[31]), .b(B[31]), .out(Add[31]), .cin(adder_5_cout), .cout(adder_6_cout));
  xor xor_1 (xor_1_out, adder_1_cout, adder_2_cout);
  Multiplexer multiplexer_3 (.in0(xor_1_out), .in1(xor_2_out), .out(multiplexer_3_out), .sel(H));
  xor xor_2 (xor_2_out, adder_3_cout, adder_4_cout);
  xor xor_3 (xor_3_out, adder_5_cout, adder_6_cout);
  Multiplexer multiplexer_4 (.in0(multiplexer_3_out), .in1(xor_3_out), .out(V), .sel(W));
endmodule
