// Logisim project bit32.6.1.circ as structural Verilog: 4 circuits, main circuit main
module main (
);

  wire ALU, and_1_out, and_2_out, and_4_out, and_6_out, and_8_out, and_10_out, and_11_out, and_12_out,
       and_13_out, and_15_out, and_16_out, button_1_out, button_2_out, button_3_out, Carry, Clk, clock_1_out,
       Cmp, counter_2_carry, demultiplexer_1_out0, demultiplexer_1_out1, demultiplexer_2_out0,
       demultiplexer_2_out1, demultiplexer_2_out2, demultiplexer_2_out3, demultiplexer_2_out4,
       demultiplexer_2_out5, demultiplexer_2_out6, demultiplexer_2_out7, demultiplexer_2_out8,
       demultiplexer_2_out9, demultiplexer_2_out10, demultiplexer_2_out11, demultiplexer_2_out12,
       demultiplexer_2_out13, demultiplexer_2_out14, demultiplexer_2_out15, Exec, H, Halt, Imm, Int, IntEn,
       j_k_ff_1_q, j_k_ff_1_qn, Jump, Latch, Link, Load, Mode, multiplexer_23_out, myadder_1_v, not_1_out,
       not_2_out, not_3_out, not_4_out, not_5_out, not_6_out, not_7_out, or_1_out, or_2_out, or_3_out,
       or_5_out, or_6_out, or_8_out, or_9_out, or_10_out, or_11_out, or_12_out, or_13_out, or_14_out,
       or_16_out, ram_1_p2, Reset, RW, Stack, Update, W, Word, xnor_1_out, xor_1_out, xor_3_out;
  wire [2:0] CVNZ;
  wire [3:0] Cond, Flags, Rd, Rs, Rs2;
  wire [4:0] multiplexer_21_out, Op5;
  wire [6:0] keyboard_1_data;
  wire [7:0] undriven, undriven_2, undriven_3, undriven_4;
  wire [26:0] multiplexer_21_out_2;
  wire [26:12] register_1_q;
  wire [31:0] A_q, adder_1_out, adder_2_out, adder_3_out, adder_4_out, Addr, and_14_out, B_q, Base,
       bit_extender_1_out, bit_extender_2_out, bit_extender_3_out, bit_extender_5_out, bit_extender_6_out,
       C_q, D_q, Data, Din, divider_1_out, divider_1_rem, Dout, E_q, F_q, fpadder_1_out, fpdivider_1_out,
       fpmultiplier_1_out, fpnegator_1_p2, fpsubtractor_1_out, fptoint_1_p2, G_q, H_q, I_q, ILR_q, Imm8,
       Imm24, Inst, inttofp_1_p2, J_q, K_q, LR_q, multiplexer_2_out, multiplexer_3_out, multiplexer_4_out,
       multiplexer_6_out, multiplexer_7_out, multiplexer_8_out, multiplexer_9_out, multiplexer_10_out,
       multiplexer_11_out, multiplexer_15_out, multiplexer_16_out, multiplexer_20_out, multiplexer_22_out,
       multiplexer_24_out, multiplier_1_out, myadder_1_add, negator_1_out, not_9_out, Offset, or_15_out, PC,
       Primary, shifter_1_out, shifter_2_out, shifter_3_out, shifter_4_out, shifter_5_out, SP, SP_q,
       xor_2_out;
  wire [31:5] SR_q;

  Multiplexer #(.select(4)) multiplexer_1 (
    .in0(1'b0), .in1(CVNZ[0]), .in2(not_1_out), .in3(CVNZ[1]), .in4(not_2_out), .in5(CVNZ[2]),
    .in6(not_3_out), .in7(Carry), .in8(not_4_out), .in9(and_1_out), .in10(or_1_out), .in11(or_3_out),
    .in12(xor_1_out), .in13(and_2_out), .in14(xnor_1_out), .in15(1'b1), .out(Exec), .sel(Cond));
  not not_1 (not_1_out, CVNZ[0]);
  not not_2 (not_2_out, CVNZ[1]);
  not not_3 (not_3_out, CVNZ[2]);
  not not_4 (not_4_out, Carry);
  and and_1 (and_1_out, ~CVNZ[0], Carry);  // AND_Gate
  or or_1 (or_1_out, CVNZ[0], ~Carry);  // OR_Gate
  not not_5 (not_5_out, Addr[31]);
  or or_2 (or_2_out, H, W);
  Demultiplexer #(.select(2)) demultiplexer_1 (
    .out0(demultiplexer_1_out0), .out1(demultiplexer_1_out1), .in(Addr[31]), .sel(Addr[1:0]));  // open: out2, out3
  xor xor_1 (xor_1_out, CVNZ[1], CVNZ[2]);
  or or_3 (or_3_out, CVNZ[0], xor_1_out);
  and and_2 (and_2_out, ~CVNZ[0], xnor_1_out);  // AND_Gate
  or or_4 (Reset, button_1_out, button_2_out);
  Button button_1 (.out(button_1_out));
  // RAM #(.addrWidth(24), .clearpin("true"), .enables("line"), .line("quad"), .misaligned("true"), .trigger("falling")) ram_1: pin names not known; wires that end beside it: Addr[23:0], ram_1_p2, or_2_out, W, Clk, Dout[7:0], Dout[15:8], Dout[23:16], Dout[31:24], button_1_out
  and and_3 (ram_1_p2, not_5_out, RW);
  TTY #(.trigger("falling")) tty_1 (.data(Dout[6:0]), .clk(Clk), .we(demultiplexer_1_out0), .clr(Reset));
  Counter #(.max('hffffffff), .width(32)) counter_1 (
    .clr(Reset), .up(1'b1), .count(1'b1), .clk(Clk));  // open: load, D, carry, Q
  xnor xnor_1 (xnor_1_out, CVNZ[1], CVNZ[2]);
  Button button_2 (.out(button_2_out));
  and and_4 (and_4_out, Clk, demultiplexer_1_out1);
  Keyboard #(.trigger("falling")) keyboard_1 (
    .clk(and_4_out), .re(demultiplexer_1_out1), .clr(Reset), .data(keyboard_1_data));  // open: avail
  and and_5 (Clk, ~Halt, or_5_out);  // AND_Gate
  or or_5 (or_5_out, clock_1_out, button_3_out);
  Clock clock_1 (.out(clock_1_out));
  Button button_3 (.out(button_3_out));
  assign bit_extender_1_out = {{25{1'b0}}, keyboard_1_data};  // Bit_Extender bit_extender_1
  and and_6 (and_6_out, ~RW, not_5_out);  // AND_Gate
  assign Din = and_6_out ? {undriven_4, undriven_3, undriven_2, undriven} : 32'bz;  // Controlled_Buffer controlled_buffer_1
  assign Din = demultiplexer_1_out1 ? bit_extender_1_out : 32'bz;  // Controlled_Buffer controlled_buffer_2
  assign bit_extender_2_out = {{24{1'b0}}, Data[7:0]};  // Bit_Extender bit_extender_2
  assign bit_extender_3_out = {{16{1'b0}}, Data[15:0]};  // Bit_Extender bit_extender_3
  // Probe on PC
  Demultiplexer #(.select(4)) demultiplexer_2 (
    .out0(demultiplexer_2_out0), .out1(demultiplexer_2_out1), .out2(demultiplexer_2_out2),
    .out3(demultiplexer_2_out3), .out4(demultiplexer_2_out4), .out5(demultiplexer_2_out5),
    .out6(demultiplexer_2_out6), .out7(demultiplexer_2_out7), .out8(demultiplexer_2_out8),
    .out9(demultiplexer_2_out9), .out10(demultiplexer_2_out10), .out11(demultiplexer_2_out11),
    .out12(demultiplexer_2_out12), .out13(demultiplexer_2_out13), .out14(demultiplexer_2_out14),
    .out15(demultiplexer_2_out15), .in(Latch), .sel(Rd));
  Multiplexer #(.width(32)) multiplexer_2 (
    .in0(bit_extender_2_out), .in1(bit_extender_3_out), .out(multiplexer_2_out), .sel(H));
  Multiplexer #(.width(32)) multiplexer_3 (.in0(multiplexer_2_out), .in1(Data), .out(multiplexer_3_out), .sel(W));
  Adder #(.width(32)) adder_1 (.a(Base), .b(multiplexer_4_out), .out(adder_1_out));  // open: cin, cout
  Multiplexer #(.width(32)) multiplexer_4 (.in0(Offset), .in1(Imm8), .out(multiplexer_4_out), .sel(Imm));
  assign Data = or_6_out ? Din : 32'bz;  // Controlled_Buffer controlled_buffer_3
  or or_6 (or_6_out, not_6_out, or_8_out);
  and and_7 (Link, Mode, or_9_out);
  or or_7 (Latch, or_8_out, and_12_out);
  Register #(.trigger("falling"), .width(32)) A (
    .D(multiplexer_3_out), .en(demultiplexer_2_out0), .clk(Clk), .Q(A_q), .clr(Reset));
  Register #(.trigger("falling"), .width(32)) B (
    .D(multiplexer_3_out), .en(demultiplexer_2_out1), .clk(Clk), .Q(B_q), .clr(Reset));
  Register #(.trigger("falling"), .width(32)) C (
    .D(multiplexer_3_out), .en(demultiplexer_2_out2), .clk(Clk), .Q(C_q), .clr(Reset));
  Register #(.trigger("falling"), .width(32)) D (
    .D(multiplexer_3_out), .en(demultiplexer_2_out3), .clk(Clk), .Q(D_q), .clr(Reset));
  Multiplexer #(.width(32)) multiplexer_5 (.in0(PC), .in1(multiplexer_6_out), .out(Addr), .sel(and_8_out));
  Multiplexer #(.width(32)) multiplexer_6 (.in0(adder_1_out), .in1(SP), .out(multiplexer_6_out), .sel(Stack));
  and and_8 (and_8_out, Clk, j_k_ff_1_qn, Load);
  and and_9 (RW, Clk, Load, Mode);
  assign Dout = RW ? Primary : 32'bz;  // Controlled_Buffer controlled_buffer_4
  not not_6 (not_6_out, Clk);
  and and_10 (and_10_out, Load, ~Mode);  // AND_Gate
  or or_8 (or_8_out, and_10_out, and_11_out);
  or or_9 (or_9_out, Jump, and_11_out);
  and and_11 (and_11_out, j_k_ff_1_q, Word);
  and and_12 (and_12_out, ALU, ~Cmp);  // AND_Gate
  J_K_Flip_Flop #(.trigger("falling")) j_k_ff_1 (
    .J(Word), .K(Word), .clk(Clk), .Q(j_k_ff_1_q), .Qn(j_k_ff_1_qn), .reset(Reset));  // open: preset
  Register #(.trigger("falling"), .width(32)) E (
    .D(multiplexer_3_out), .en(demultiplexer_2_out4), .clk(Clk), .Q(E_q), .clr(Reset));
  Register #(.trigger("falling"), .width(32)) F (
    .D(multiplexer_3_out), .en(demultiplexer_2_out5), .clk(Clk), .Q(F_q), .clr(Reset));
  Register #(.trigger("falling"), .width(32)) G (
    .D(multiplexer_3_out), .en(demultiplexer_2_out6), .clk(Clk), .Q(G_q), .clr(Reset));
  Register #(.trigger("falling"), .width(32)) u_H (
    .D(multiplexer_3_out), .en(demultiplexer_2_out7), .clk(Clk), .Q(H_q), .clr(Reset));
  Register #(.width(32)) register_1 (
    .D(Inst), .en(j_k_ff_1_qn), .clk(Clk),
    .Q({Cond, Mode, register_1_q[26:24], W, H, Op5, register_1_q[16:12], Rs2, Rs, Rd}), .clr(Reset));
  and and_13 (and_13_out, j_k_ff_1_qn, IntEn);
  Multiplexer #(.width(32)) multiplexer_7 (
    .in0(adder_3_out), .in1(multiplexer_3_out), .out(multiplexer_7_out), .sel(demultiplexer_2_out11));
  Multiplexer #(.width(32)) multiplexer_8 (
    .in0({SR_q, Halt, Flags}), .in1(multiplexer_3_out), .out(multiplexer_8_out), .sel(demultiplexer_2_out12));
  Multiplexer #(.width(32)) multiplexer_9 (
    .in0(multiplexer_15_out), .in1(multiplexer_3_out), .out(multiplexer_9_out), .sel(demultiplexer_2_out13));
  Multiplexer #(.width(32)) multiplexer_10 (
    .in0(adder_4_out), .in1(multiplexer_3_out), .out(multiplexer_10_out), .sel(demultiplexer_2_out14));
  PLA #(.in_width(4), .out_width(7), .\table ("0xxx 0000000\n1000 0000001\n1001 0000010\n1010 0000100\n1011 0001100\n1100 0010000\n1101 0011000\n1110 0110000\n1111 1000000")) pla_1 (
    .in({Exec, register_1_q[26:24]}), .out({Word, Stack, Load, Imm, ALU, Int, Jump}));
  Counter counter_2 (
    .clr(Reset), .load(1'b0), .up(and_13_out), .count(and_13_out), .clk(Clk), .carry(counter_2_carry));  // open: D, Q
  Register #(.trigger("falling"), .width(32)) I (
    .D(multiplexer_3_out), .en(demultiplexer_2_out8), .clk(Clk), .Q(I_q), .clr(Reset));
  Register #(.trigger("falling"), .width(32)) J (
    .D(multiplexer_3_out), .en(demultiplexer_2_out9), .clk(Clk), .Q(J_q), .clr(Reset));
  Register #(.trigger("falling"), .width(32)) K (
    .D(multiplexer_3_out), .en(demultiplexer_2_out10), .clk(Clk), .Q(K_q), .clr(Reset));
  Register #(.trigger("falling"), .width(32)) u_SP (
    .D(multiplexer_7_out), .en(or_10_out), .clk(Clk), .Q(SP_q), .clr(Reset));
  or or_10 (or_10_out, demultiplexer_2_out11, Stack);
  Register #(.trigger("falling"), .width(32)) SR (
    .D(multiplexer_8_out), .en(or_11_out), .clk(Clk), .Q({SR_q, Halt, Carry, CVNZ}), .clr(Reset));
  or or_11 (or_11_out, demultiplexer_2_out12, Update);
  Register #(.trigger("falling"), .width(32)) ILR (
    .D(multiplexer_9_out), .en(or_12_out), .clk(Clk), .Q(ILR_q), .clr(Reset));
  or or_12 (or_12_out, demultiplexer_2_out13, Int);
  Register #(.trigger("falling"), .width(32)) LR (
    .D(multiplexer_10_out), .en(or_13_out), .clk(Clk), .Q(LR_q), .clr(Reset));
  or or_13 (or_13_out, demultiplexer_2_out14, Link);
  Register #(.trigger("falling"), .width(32)) u_PC (
    .D(multiplexer_11_out), .en(not_7_out), .clk(Clk), .Q(PC), .clr(Reset));
  Multiplexer #(.width(32)) multiplexer_11 (
    .in0(multiplexer_20_out), .in1(multiplexer_3_out), .out(multiplexer_11_out), .sel(demultiplexer_2_out15));
  not not_7 (not_7_out, Halt);
  assign Imm24 = {{8{W}}, {W, H, Op5, register_1_q[16:12], Rs2, Rs, Rd}};  // Bit_Extender bit_extender_4
  assign bit_extender_5_out = {{24{register_1_q[15]}}, {register_1_q[15:12], Rs2}};  // Bit_Extender bit_extender_5
  assign bit_extender_6_out = {{24{1'b0}}, {register_1_q[15:12], Rs2}};  // Bit_Extender bit_extender_6
  Multiplexer #(.width(32)) multiplexer_12 (.in0(Data), .in1(32'hf1000044), .out(Inst), .sel(counter_2_carry));
  Adder #(.width(32)) adder_2 (.a(PC), .b(Imm24), .out(adder_2_out));  // open: cin, cout
  Multiplexer #(.width(32)) multiplexer_13 (
    .in0(bit_extender_5_out), .in1(bit_extender_6_out), .out(Imm8), .sel(register_1_q[16]));
  Multiplexer #(.width(32)) multiplexer_14 (.in0(SP_q), .in1(adder_3_out), .out(SP), .sel(Mode));
  Adder #(.width(32)) adder_3 (.a(SP_q), .b(Imm8), .out(adder_3_out));  // open: cin, cout
  not not_8 (IntEn, SR_q[5]);
  Multiplexer #(.width(32)) multiplexer_15 (.in0(PC), .in1(adder_4_out), .out(multiplexer_15_out), .sel(Mode));
  Adder #(.width(32)) adder_4 (.a(PC), .b(32'h4), .out(adder_4_out));  // open: cin, cout
  Multiplexer #(.width(32)) multiplexer_16 (.in0(adder_2_out), .in1(Imm24), .out(multiplexer_16_out), .sel(Int));
  Multiplexer #(.select(4), .width(32)) multiplexer_17 (
    .in0(A_q), .in1(B_q), .in2(C_q), .in3(D_q), .in4(E_q), .in5(F_q), .in6(G_q), .in7(H_q), .in8(I_q),
    .in9(J_q), .in10(K_q), .in11(SP_q), .in12({SR_q, Halt, Carry, CVNZ}), .in13(ILR_q), .in14(LR_q),
    .in15(PC), .out(Primary), .sel(Rd));
  Multiplexer #(.select(4), .width(32)) multiplexer_18 (
    .in0(A_q), .in1(B_q), .in2(C_q), .in3(D_q), .in4(E_q), .in5(F_q), .in6(G_q), .in7(H_q), .in8(I_q),
    .in9(J_q), .in10(K_q), .in11(SP_q), .in12({SR_q, Halt, Carry, CVNZ}), .in13(ILR_q), .in14(LR_q),
    .in15(PC), .out(Base), .sel(Rs));
  Multiplexer #(.select(4), .width(32)) multiplexer_19 (
    .in0(A_q), .in1(B_q), .in2(C_q), .in3(D_q), .in4(E_q), .in5(F_q), .in6(G_q), .in7(H_q), .in8(I_q),
    .in9(J_q), .in10(K_q), .in11(SP_q), .in12({SR_q, Halt, Carry, CVNZ}), .in13(ILR_q), .in14(LR_q),
    .in15(PC), .out(Offset), .sel(Rs2));
  Multiplexer #(.width(32)) multiplexer_20 (
    .in0(adder_4_out), .in1(multiplexer_16_out), .out(multiplexer_20_out), .sel(or_14_out));
  or or_14 (or_14_out, Jump, Int);
  Multiplexer #(.width(32)) multiplexer_21 (
    .in0(Offset), .in1(Imm8), .out({multiplexer_21_out_2, multiplexer_21_out}), .sel(Imm));
  assign not_9_out = ~{multiplexer_21_out_2, multiplexer_21_out};  // NOT_Gate not_9, 32 bits wide
  Multiplexer #(.width(32)) multiplexer_22 (
    .in0({multiplexer_21_out_2, multiplexer_21_out}), .in1(not_9_out), .out(multiplexer_22_out), .sel(Op5[2]));
  Negator #(.width(32)) negator_1 (.in({multiplexer_21_out_2, multiplexer_21_out}), .out(negator_1_out));
  assign and_14_out = Base & {multiplexer_21_out_2, multiplexer_21_out};  // AND_Gate and_14, 32 bits wide
  assign or_15_out = Base | {multiplexer_21_out_2, multiplexer_21_out};  // OR_Gate or_15, 32 bits wide
  assign xor_2_out = Base ^ {multiplexer_21_out_2, multiplexer_21_out};  // XOR_Gate xor_2, 32 bits wide
  // IntToFP #(.width(32)) inttofp_1: pin names not known; wires that end beside it: {multiplexer_21_out_2, multiplexer_21_out}, inttofp_1_p2
  FPAdder fpadder_1 (.a(Base), .b({multiplexer_21_out_2, multiplexer_21_out}), .out(fpadder_1_out));
  FPSubtractor fpsubtractor_1 (.a(Base), .b({multiplexer_21_out_2, multiplexer_21_out}), .out(fpsubtractor_1_out));
  // FPToInt #(.mode("floor"), .width(32)) fptoint_1: pin names not known; wires that end beside it: {multiplexer_21_out_2, multiplexer_21_out}, fptoint_1_p2
  // FPNegator fpnegator_1: pin names not known; wires that end beside it: {multiplexer_21_out_2, multiplexer_21_out}, fpnegator_1_p2
  FPMultiplier fpmultiplier_1 (.a(Base), .b({multiplexer_21_out_2, multiplexer_21_out}), .out(fpmultiplier_1_out));
  FPDivider fpdivider_1 (.a(Base), .b({multiplexer_21_out_2, multiplexer_21_out}), .out(fpdivider_1_out));
  Multiplier #(.width(32)) multiplier_1 (
    .a(Base), .b({multiplexer_21_out_2, multiplexer_21_out}), .out(multiplier_1_out));  // open: cin, cout
  Divider #(.width(32)) divider_1 (
    .a(Base), .b({multiplexer_21_out_2, multiplexer_21_out}), .out(divider_1_out), .rem(divider_1_rem));  // open: upper
  Shifter #(.shift("lr"), .width(32)) shifter_1 (.in(Base), .\dist (multiplexer_21_out), .out(shifter_1_out));
  Shifter #(.width(32)) shifter_2 (.in(Base), .\dist (multiplexer_21_out), .out(shifter_2_out));
  Shifter #(.shift("ar"), .width(32)) shifter_3 (.in(Base), .\dist (multiplexer_21_out), .out(shifter_3_out));
  Shifter #(.shift("rr"), .width(32)) shifter_4 (.in(Base), .\dist (multiplexer_21_out), .out(shifter_4_out));
  Shifter #(.shift("rl"), .width(32)) shifter_5 (.in(Base), .\dist (multiplexer_21_out), .out(shifter_5_out));
  xor xor_3 (xor_3_out, Op5[2], Carry);
  Multiplexer multiplexer_23 (.in0(Op5[2]), .in1(xor_3_out), .out(multiplexer_23_out), .sel(and_15_out));
  MyAdder myadder_1 (
    .H(H), .W(W), .A(Base), .B(multiplexer_22_out), .Cin(multiplexer_23_out), .Cout(Flags[3]),
    .Add(myadder_1_add), .V(myadder_1_v));
  Multiplexer #(.select(5), .width(32)) multiplexer_24 (
    .in0({multiplexer_21_out_2, multiplexer_21_out}), .in1(myadder_1_add), .in2(myadder_1_add),
    .in3(myadder_1_add), .in4(negator_1_out), .in5(myadder_1_add), .in6(myadder_1_add), .in7(myadder_1_add),
    .in8(not_9_out), .in9(negator_1_out), .in10(and_14_out), .in11(and_14_out), .in12(or_15_out),
    .in14(xor_2_out), .in15(xor_2_out), .in16(inttofp_1_p2), .in17(fpadder_1_out), .in18(fpsubtractor_1_out),
    .in19(fpsubtractor_1_out), .in20(fptoint_1_p2), .in21(fpnegator_1_p2), .in22(fpmultiplier_1_out),
    .in23(fpdivider_1_out), .in24(multiplier_1_out), .in25(divider_1_out), .in26(divider_1_rem),
    .in27(shifter_1_out), .in28(shifter_2_out), .in29(shifter_3_out), .in30(shifter_4_out),
    .in31(shifter_5_out), .out(multiplexer_24_out), .sel(Op5));  // open: in13
  and and_15 (and_15_out, Op5[1], ~Op5[0]);  // AND_Gate
  assign Data = and_16_out ? multiplexer_24_out : 32'bz;  // Controlled_Buffer controlled_buffer_5
  and and_16 (and_16_out, Clk, ALU);
  SignedCMP signedcmp_1 (.Data(multiplexer_24_out), .H(H), .W(W), .Z(Flags[0]), .N(Flags[1]));
  and and_17 (Flags[2], myadder_1_v, ~Op5[4]);  // AND_Gate
  and and_18 (Cmp, Op5[0], Op5[1], ~Op5[4]);  // AND_Gate
  and and_19 (Update, ALU, or_16_out);
  or or_16 (or_16_out, Mode, Cmp);

  // Other names for the same wires on the sheet: CVNZ[3] = Carry
endmodule

module MyAdder (
  input  [31:0] A,
  input  [31:0] B,
  input  Cin,
  input  H,
  input  W,
  output V,
  output Cout,
  output [31:0] Add
);

  wire adder_1_cout, adder_2_cout, adder_3_cout, adder_4_cout, adder_5_cout, adder_6_cout, multiplexer_1_out,
       multiplexer_3_out, xor_1_out, xor_2_out, xor_3_out;

  Multiplexer multiplexer_1 (.in0(adder_2_cout), .in1(adder_4_cout), .out(multiplexer_1_out), .sel(H));
  Multiplexer multiplexer_2 (.in0(multiplexer_1_out), .in1(adder_6_cout), .out(Cout), .sel(W));
  Adder #(.width(7)) adder_1 (.a(A[6:0]), .b(B[6:0]), .out(Add[6:0]), .cin(Cin), .cout(adder_1_cout));
  Adder #(.width(1)) adder_2 (.a(A[7]), .b(B[7]), .out(Add[7]), .cin(adder_1_cout), .cout(adder_2_cout));
  Adder #(.width(7)) adder_3 (.a(A[14:8]), .b(B[14:8]), .out(Add[14:8]), .cin(adder_2_cout), .cout(adder_3_cout));
  Adder #(.width(1)) adder_4 (.a(A[15]), .b(B[15]), .out(Add[15]), .cin(adder_3_cout), .cout(adder_4_cout));
  Adder #(.width(15)) adder_5 (.a(A[30:16]), .b(B[30:16]), .out(Add[30:16]), .cin(adder_4_cout), .cout(adder_5_cout));
  Adder #(.width(1)) adder_6 (.a(A[31]), .b(B[31]), .out(Add[31]), .cin(adder_5_cout), .cout(adder_6_cout));
  xor xor_1 (xor_1_out, adder_1_cout, adder_2_cout);
  Multiplexer multiplexer_3 (.in0(xor_1_out), .in1(xor_2_out), .out(multiplexer_3_out), .sel(H));
  xor xor_2 (xor_2_out, adder_3_cout, adder_4_cout);
  xor xor_3 (xor_3_out, adder_5_cout, adder_6_cout);
  Multiplexer multiplexer_4 (.in0(multiplexer_3_out), .in1(xor_3_out), .out(V), .sel(W));
endmodule

module SignedCMP (
  input  [31:0] Data,
  input  H,
  input  W,
  output Z,
  output N
);

  wire comparator_1_eq, comparator_2_eq, comparator_3_eq, multiplexer_1_out, multiplexer_3_out;

  Comparator comparator_1 (.a(Data[7:0]), .b({8{1'b0}}), .eq(comparator_1_eq));  // open: gt, lt
  Comparator #(.width(16)) comparator_2 (.a(Data[15:0]), .b({16{1'b0}}), .eq(comparator_2_eq));  // open: gt, lt
  Comparator #(.width(32)) comparator_3 (.a(Data), .b({32{1'b0}}), .eq(comparator_3_eq));  // open: gt, lt
  Multiplexer multiplexer_1 (.in0(comparator_1_eq), .in1(comparator_2_eq), .out(multiplexer_1_out), .sel(H));
  Multiplexer multiplexer_2 (.in0(multiplexer_1_out), .in1(comparator_3_eq), .out(Z), .sel(W));
  Multiplexer multiplexer_3 (.in0(Data[7]), .in1(Data[15]), .out(multiplexer_3_out), .sel(H));
  Multiplexer multiplexer_4 (.in0(multiplexer_3_out), .in1(Data[31]), .out(N), .sel(W));
endmodule

module Video (
);

  wire button_1_out, clock_1_out, counter_1_carry;
  wire [5:0] counter_1_q, counter_2_q;
  wire [15:0] bit_extender_1_out, ram_1_p1;
  wire [23:0] rgb_video_1_p6;

  Clock clock_1 (.out(clock_1_out));
  Button button_1 (.out(button_1_out));
  Counter #(.max('h3f), .width(6)) counter_1 (
    .clr(button_1_out), .up(1'b1), .count(1'b1), .clk(clock_1_out), .carry(counter_1_carry), .Q(counter_1_q));  // open: load, D
  Counter #(.max('h3f), .width(6)) counter_2 (
    .clr(button_1_out), .up(counter_1_carry), .count(counter_1_carry), .clk(clock_1_out), .Q(counter_2_q));  // open: load, D, carry
  Shifter shifter_1 ();  // open: in, dist, out
  // RGB_Video #(.height(64), .scale(4), .width(64)) rgb_video_1: pin names not known; wires that end beside it: button_1_out, clock_1_out, clock_1_out, counter_1_q, counter_2_q, rgb_video_1_p6
  assign bit_extender_1_out = {{4{counter_2_q[5]}}, {counter_2_q, counter_1_q}};  // Bit_Extender bit_extender_1
  // RAM #(.addrWidth(16), .enables("line"), .line("quad"), .misaligned("true"), .trigger("falling")) ram_1: pin names not known; wires that end beside it: ram_1_p1, 1'b0, 1'b1, 1'b0, clock_1_out
  Shifter #(.width(16)) shifter_2 (.in(bit_extender_1_out), .\dist (4'b0010), .out(ram_1_p1));
endmodule
