// Logisim project bit32.circ as structural Verilog: 2 circuits, main circuit main
module main (
  input  in_1,
  input  in_2
);

  wire ALU, and_1_out, and_2_out, and_3_out, and_4_out, and_5_out, and_6_out, and_7_out, and_8_out,
       and_9_out, and_10_out, and_11_out, and_12_out, and_13_out, and_14_out, and_15_out, and_16_out,
       and_17_out, and_18_out, and_19_out, and_20_out, and_21_out, and_22_out, and_25_out, and_26_out,
       and_27_out, button_1_out, button_2_out, button_3_out, Clk, clock_1_out, Cmp, controlled_buffer_6_out,
       demultiplexer_1_out0, demultiplexer_1_out1, demultiplexer_1_out2, demultiplexer_1_out3,
       demultiplexer_1_out4, demultiplexer_1_out5, demultiplexer_1_out6, demultiplexer_1_out7,
       demultiplexer_1_out8, demultiplexer_1_out9, demultiplexer_1_out10, demultiplexer_1_out11,
       demultiplexer_1_out12, demultiplexer_1_out13, demultiplexer_1_out14, demultiplexer_1_out15, Exec, F,
       Int, j_k_ff_1_q, j_k_ff_1_qn, Jump, Latch, Load, not_1_out, not_2_out, not_3_out, not_4_out,
       not_5_out, or_1_out, or_2_out, or_3_out, or_5_out, or_8_out, or_11_out, Reset, RW, Stack, undriven_3,
       undriven_4, Word, xnor_1_out, xnor_2_out, xor_1_out, xor_2_out;
  wire [3:0] comparator_1_eq, Cond, CVNZ;
  wire [4:0] multiplexer_11_out;
  wire [6:2] pla_1_out;
  wire [7:0] controlled_buffer_1_out, register_3_q, register_4_q, register_9_q, register_10_q, register_15_q,
       register_16_q, register_21_q, register_22_q, undriven_5, undriven_6, undriven_7, undriven_8;
  wire [15:0] controlled_buffer_2_out, r0_q, r1_q, register_2_q, register_5_q, register_7_q, register_8_q,
       register_11_q, register_13_q, register_14_q, register_17_q, register_18_q, register_20_q;
  wire [22:0] Code24;
  wire [26:0] multiplexer_11_out_2;
  wire [26:24] IR_q;
  wire [31:0] adder_1_out, adder_2_out, adder_3_out, Addr, and_24_out, Base, Const8, Data, Din,
       divider_1_out, divider_1_rem, Dout, f0_q, f1_q, f2_q, f3_q, fp_q, fpadder_1_out, fpdivider_1_out,
       fpmultiplier_1_out, fpnegator_1_p2, fpsubtractor_1_out, fptoint_1_p2, inttofp_1_p2, lr_q,
       multiplexer_2_out, multiplexer_3_out, multiplexer_4_out, multiplexer_8_out, multiplexer_9_out,
       multiplexer_12_out, multiplexer_13_out, multiplier_1_out, myadder_1_add, negator_1_out, not_6_out,
       Offset, Offset24, or_9_out, PC, Primary, shifter_1_out, shifter_2_out, shifter_3_out, shifter_4_out,
       shifter_5_out, SP, undriven, undriven_9, xor_3_out;
  wire [31:8] undriven_2;

  Multiplexer #(.select(4)) multiplexer_1 (
    .in0(1'b0), .in1(CVNZ[0]), .in2(not_1_out), .in3(CVNZ[1]), .in4(not_2_out), .in5(CVNZ[2]),
    .in6(not_3_out), .in7(CVNZ[3]), .in8(not_4_out), .in9(and_1_out), .in10(or_1_out), .in11(xor_1_out),
    .in12(xnor_1_out), .in13(or_2_out), .in14(and_6_out), .in15(1'b1), .out(Exec), .sel(Cond));
  not not_1 (not_1_out, CVNZ[0]);
  not not_2 (not_2_out, CVNZ[1]);
  not not_3 (not_3_out, CVNZ[2]);
  Demultiplexer #(.select(4)) demultiplexer_1 (
    .out0(demultiplexer_1_out0), .out1(demultiplexer_1_out1), .out2(demultiplexer_1_out2),
    .out3(demultiplexer_1_out3), .out4(demultiplexer_1_out4), .out5(demultiplexer_1_out5),
    .out6(demultiplexer_1_out6), .out7(demultiplexer_1_out7), .out8(demultiplexer_1_out8),
    .out9(demultiplexer_1_out9), .out10(demultiplexer_1_out10), .out11(demultiplexer_1_out11),
    .out12(demultiplexer_1_out12), .out13(demultiplexer_1_out13), .out14(demultiplexer_1_out14),
    .out15(demultiplexer_1_out15), .in(Latch), .sel(Code24[3:0]));
  not not_4 (not_4_out, CVNZ[3]);
  and and_1 (and_1_out, ~CVNZ[0], CVNZ[3]);  // AND_Gate
  or or_1 (or_1_out, CVNZ[0], ~CVNZ[3]);  // OR_Gate
  and and_2 (and_2_out, in_2, demultiplexer_1_out0);
  and and_3 (and_3_out, in_1, demultiplexer_1_out0);
  and and_4 (and_4_out, in_2, demultiplexer_1_out1);
  and and_5 (and_5_out, in_1, demultiplexer_1_out1);
  xor xor_1 (xor_1_out, CVNZ[1], CVNZ[2]);
  xnor xnor_1 (xnor_1_out, CVNZ[1], CVNZ[2]);
  Register #(.trigger("falling"), .width(16)) r0 (
    .D(undriven[31:16]), .en(and_2_out), .clk(Clk), .Q(r0_q), .clr(Reset));
  Register #(.trigger("falling")) register_1 (
    .D(undriven[15:8]), .en(and_3_out), .clk(Clk), .Q(register_2_q[15:8]), .clr(Reset));
  Register #(.trigger("falling")) register_2 (
    .D(undriven[7:0]), .en(demultiplexer_1_out0), .clk(Clk), .Q(register_2_q[7:0]), .clr(Reset));
  Register #(.trigger("falling"), .width(16)) r1 (
    .D(undriven[31:16]), .en(and_4_out), .clk(Clk), .Q(r1_q), .clr(Reset));
  Register #(.trigger("falling")) register_3 (
    .D(undriven[15:8]), .en(and_5_out), .clk(Clk), .Q(register_3_q), .clr(Reset));
  Register #(.trigger("falling")) register_4 (
    .D(undriven[7:0]), .en(demultiplexer_1_out1), .clk(Clk), .Q(register_4_q), .clr(Reset));
  xor xor_2 (xor_2_out, CVNZ[1], CVNZ[2]);
  or or_2 (or_2_out, CVNZ[0], xor_2_out);
  xnor xnor_2 (xnor_2_out, CVNZ[1], CVNZ[2]);
  and and_6 (and_6_out, ~CVNZ[0], xnor_2_out);  // AND_Gate
  and and_7 (and_7_out, in_2, demultiplexer_1_out2);
  and and_8 (and_8_out, in_2, demultiplexer_1_out2);
  and and_9 (and_9_out, in_2, demultiplexer_1_out3);
  and and_10 (and_10_out, in_2, demultiplexer_1_out3);
  Register #(.trigger("falling"), .width(16)) register_5 (
    .D(undriven[31:16]), .en(and_7_out), .clk(Clk), .Q(register_5_q), .clr(Reset));
  Register #(.trigger("falling")) register_6 (
    .D(undriven[15:8]), .en(and_8_out), .clk(Clk), .Q(register_7_q[15:8]), .clr(Reset));
  Register #(.trigger("falling")) register_7 (
    .D(undriven[7:0]), .en(demultiplexer_1_out2), .clk(Clk), .Q(register_7_q[7:0]), .clr(Reset));
  Register #(.trigger("falling"), .width(16)) register_8 (
    .D(undriven[31:16]), .en(and_9_out), .clk(Clk), .Q(register_8_q), .clr(Reset));
  Register #(.trigger("falling")) register_9 (
    .D(undriven[15:8]), .en(and_10_out), .clk(Clk), .Q(register_9_q), .clr(Reset));
  Register #(.trigger("falling")) register_10 (
    .D(undriven[7:0]), .en(demultiplexer_1_out3), .clk(Clk), .Q(register_10_q), .clr(Reset));
  and and_11 (and_11_out, in_2, demultiplexer_1_out4);
  and and_12 (and_12_out, in_1, demultiplexer_1_out4);
  and and_13 (and_13_out, in_2, demultiplexer_1_out5);
  and and_14 (and_14_out, in_1, demultiplexer_1_out5);
  Register #(.trigger("falling"), .width(16)) register_11 (
    .D(undriven[31:16]), .en(and_11_out), .clk(Clk), .Q(register_11_q), .clr(Reset));
  Register #(.trigger("falling")) register_12 (
    .D(undriven[15:8]), .en(and_12_out), .clk(Clk), .Q(register_13_q[15:8]), .clr(Reset));
  Register #(.trigger("falling")) register_13 (
    .D(undriven[7:0]), .en(demultiplexer_1_out4), .clk(Clk), .Q(register_13_q[7:0]), .clr(Reset));
  Register #(.trigger("falling"), .width(16)) register_14 (
    .D(undriven[31:16]), .en(and_13_out), .clk(Clk), .Q(register_14_q), .clr(Reset));
  Register #(.trigger("falling")) register_15 (
    .D(undriven[15:8]), .en(and_14_out), .clk(Clk), .Q(register_15_q), .clr(Reset));
  Register #(.trigger("falling")) register_16 (
    .D(undriven[7:0]), .en(demultiplexer_1_out5), .clk(Clk), .Q(register_16_q), .clr(Reset));
  Register #(.trigger("falling"), .width(16)) register_17 (
    .D(undriven[31:16]), .en(and_15_out), .clk(Clk), .Q(register_17_q), .clr(Reset));
  and and_15 (and_15_out, in_2, demultiplexer_1_out6);
  and and_16 (and_16_out, in_1, demultiplexer_1_out6);
  Register #(.trigger("falling"), .width(16)) register_18 (
    .D(undriven[31:16]), .en(and_17_out), .clk(Clk), .Q(register_18_q), .clr(Reset));
  and and_17 (and_17_out, in_2, demultiplexer_1_out7);
  and and_18 (and_18_out, in_1, demultiplexer_1_out7);
  Register #(.trigger("falling")) register_19 (
    .D(undriven[15:8]), .en(and_16_out), .clk(Clk), .Q(register_20_q[15:8]), .clr(Reset));
  Register #(.trigger("falling")) register_20 (
    .D(undriven[7:0]), .en(demultiplexer_1_out6), .clk(Clk), .Q(register_20_q[7:0]), .clr(Reset));
  Register #(.trigger("falling")) register_21 (
    .D(undriven[15:8]), .en(and_18_out), .clk(Clk), .Q(register_21_q), .clr(Reset));
  Register #(.trigger("falling")) register_22 (
    .D(undriven[7:0]), .en(demultiplexer_1_out7), .clk(Clk), .Q(register_22_q), .clr(Reset));
  Multiplexer #(.width(32)) multiplexer_2 (
    .in0(adder_1_out), .in1(Data), .out(multiplexer_2_out), .sel(demultiplexer_1_out14));
  or or_3 (or_3_out, demultiplexer_1_out14, Stack);
  Multiplexer #(.width(32)) multiplexer_3 (
    .in0(adder_2_out), .in1(Data), .out(multiplexer_3_out), .sel(demultiplexer_1_out15));
  Register #(.trigger("falling"), .width(32)) f0 (
    .D(Data), .en(demultiplexer_1_out8), .clk(Clk), .Q(f0_q), .clr(Reset));
  Register #(.trigger("falling"), .width(32)) f1 (
    .D(Data), .en(demultiplexer_1_out9), .clk(Clk), .Q(f1_q), .clr(Reset));
  Register #(.trigger("falling"), .width(32)) f2 (
    .D(Data), .en(demultiplexer_1_out10), .clk(Clk), .Q(f2_q), .clr(Reset));
  Register #(.trigger("falling"), .width(32)) f3 (
    .D(Data), .en(demultiplexer_1_out11), .clk(Clk), .Q(f3_q), .clr(Reset));
  Register #(.trigger("falling"), .width(32)) lr (
    .D(Data), .en(demultiplexer_1_out12), .clk(Clk), .Q(lr_q), .clr(Reset));
  Register #(.trigger("falling"), .width(32)) fp (
    .D(Data), .en(demultiplexer_1_out13), .clk(Clk), .Q(fp_q), .clr(Reset));
  Register #(.trigger("falling"), .width(32)) u_SP (
    .D(multiplexer_2_out), .en(or_3_out), .clk(Clk), .Q(SP), .clr(Reset));
  Register #(.trigger("falling"), .width(32)) u_PC (.D(multiplexer_3_out), .en(1'b1), .clk(Clk), .Q(PC), .clr(Reset));
  Adder #(.width(32)) adder_1 (.a(SP), .b(Const8), .out(adder_1_out));  // open: cin, cout
  Multiplexer #(.width(32)) multiplexer_4 (.in0(32'h4), .in1(Offset24), .out(multiplexer_4_out), .sel(Jump));
  Multiplexer #(.select(4), .width(32)) multiplexer_5 (
    .in0({r0_q, register_2_q}), .in1({r1_q, register_3_q, register_4_q}), .in2({register_5_q, register_7_q}),
    .in3({register_8_q, register_9_q, register_10_q}), .in4({register_11_q, register_13_q}),
    .in5({register_14_q, register_15_q, register_16_q}), .in6({register_17_q, register_20_q}),
    .in7({register_18_q, register_21_q, register_22_q}), .in8(f0_q), .in9(f1_q), .in10(f2_q), .in11(f3_q),
    .in12(lr_q), .in13(fp_q), .in14(SP), .in15(PC), .out(Primary), .sel(Code24[3:0]));
  Multiplexer #(.select(4), .width(32)) multiplexer_6 (
    .in0({r0_q, register_2_q}), .in1({r1_q, register_3_q, register_4_q}), .in2({register_5_q, register_7_q}),
    .in3({register_8_q, register_9_q, register_10_q}), .in4({register_11_q, register_13_q}),
    .in5({register_14_q, register_15_q, register_16_q}), .in6({register_17_q, register_20_q}),
    .in7({register_18_q, register_21_q, register_22_q}), .in8(f0_q), .in9(f1_q), .in10(f2_q), .in11(f3_q),
    .in12(lr_q), .in13(fp_q), .in14(SP), .in15(PC), .out(Base), .sel(Code24[7:4]));
  Multiplexer #(.select(4), .width(32)) multiplexer_7 (
    .in0({r0_q, register_2_q}), .in1({r1_q, register_3_q, register_4_q}), .in2({register_5_q, register_7_q}),
    .in3({register_8_q, register_9_q, register_10_q}), .in4({register_11_q, register_13_q}),
    .in5({register_14_q, register_15_q, register_16_q}), .in6({register_17_q, register_20_q}),
    .in7({register_18_q, register_21_q, register_22_q}), .in8(f0_q), .in9(f1_q), .in10(f2_q), .in11(f3_q),
    .in12(lr_q), .in13(fp_q), .in14(SP), .in15(PC), .out(Offset), .sel(Code24[11:8]));
  Adder #(.width(32)) adder_2 (.a(PC), .b(multiplexer_4_out), .out(adder_2_out));  // open: cin, cout
  assign controlled_buffer_1_out = undriven_3 ? undriven_2[15:8] : 8'bz;  // Controlled_Buffer controlled_buffer_1
  assign controlled_buffer_2_out = undriven_4 ? undriven_2[31:16] : 16'bz;  // Controlled_Buffer controlled_buffer_2
  // RAM #(.addrWidth(24), .enables("line"), .line("quad"), .misaligned("true"), .trigger("falling")) ram_1: pin names not known; wires that end beside it: Addr[23:0], RW, RW, in_1, Code24[21], Clk
  Button button_1 (.out(button_1_out));
  or or_4 (Reset, button_1_out, button_2_out);
  Button button_2 (.out(button_2_out));
  Adder #(.width(32)) adder_3 (.a(Base), .b(multiplexer_8_out), .out(adder_3_out));  // open: cin, cout
  Multiplexer #(.width(32)) multiplexer_8 (.in0(Offset), .in1(Const8), .out(multiplexer_8_out), .sel(Code24[21]));
  assign Data = or_5_out ? Din : 32'bz;  // Controlled_Buffer controlled_buffer_3
  or or_5 (or_5_out, ~Clk, or_8_out);  // OR_Gate
  or or_6 (Latch, or_8_out, and_21_out);
  or or_7 (Clk, clock_1_out, button_3_out);
  Clock clock_1 (.out(clock_1_out));
  Button button_3 (.out(button_3_out));
  not not_5 (not_5_out, RW);
  assign Din = not_5_out ? {undriven_8, undriven_7, undriven_6, undriven_5} : 32'bz;  // Controlled_Buffer controlled_buffer_4
  Multiplexer #(.width(32)) multiplexer_9 (.in0(adder_3_out), .in1(SP), .out(multiplexer_9_out), .sel(Stack));
  assign Dout = RW ? Primary : 32'bz;  // Controlled_Buffer controlled_buffer_5
  and and_19 (and_19_out, Load, ~Code24[20]);  // AND_Gate
  or or_8 (or_8_out, and_19_out, and_20_out);
  and and_20 (and_20_out, Word, j_k_ff_1_q);
  and and_21 (and_21_out, ALU, ~Cmp);  // AND_Gate
  Multiplexer #(.width(32)) multiplexer_10 (.in0(PC), .in1(multiplexer_9_out), .out(Addr), .sel(and_22_out));
  and and_22 (and_22_out, Clk, j_k_ff_1_qn, Load);
  and and_23 (RW, Clk, Load, Code24[20]);
  J_K_Flip_Flop #(.trigger("falling")) j_k_ff_1 (
    .J(Word), .K(Word), .clk(Clk), .Q(j_k_ff_1_q), .Qn(j_k_ff_1_qn), .reset(Reset));  // open: preset
  Register #(.width(32)) IR (.D(Data), .en(j_k_ff_1_qn), .clk(Clk), .Q({Cond, F, IR_q, in_2, Code24}), .clr(Reset));
  Multiplexer #(.width(32)) multiplexer_11 (
    .in0(Offset), .in1(Const8), .out({multiplexer_11_out_2, multiplexer_11_out}), .sel(Code24[21]));
  PLA #(.in_width(4), .out_width(8), .\table ("0xxx 00000000\n1000 00000001\n1001 00000010\n1010 00000000\n1011 00001000\n1100 00011000\n1101 00100000\n1110 01000000\n1111 11000000")) pla_1 (
    .in({Exec, IR_q}), .out({Word, pla_1_out[6], Int, Stack, Load, pla_1_out[2], ALU, Jump}));
  Multiplexer #(.width(32)) multiplexer_12 (
    .in0(Base), .in1(negator_1_out), .out(multiplexer_12_out), .sel(and_25_out));
  Negator #(.width(32)) negator_1 (.in({multiplexer_11_out_2, multiplexer_11_out}), .out(negator_1_out));
  assign not_6_out = ~{multiplexer_11_out_2, multiplexer_11_out};  // NOT_Gate not_6, 32 bits wide
  assign and_24_out = Base & {multiplexer_11_out_2, multiplexer_11_out};  // AND_Gate and_24, 32 bits wide
  assign or_9_out = Base | {multiplexer_11_out_2, multiplexer_11_out};  // OR_Gate or_9, 32 bits wide
  assign xor_3_out = Base ^ {multiplexer_11_out_2, multiplexer_11_out};  // XOR_Gate xor_3, 32 bits wide
  // IntToFP #(.width(32)) inttofp_1: pin names not known; wires that end beside it: {multiplexer_11_out_2, multiplexer_11_out}, inttofp_1_p2
  FPAdder fpadder_1 (.a(Base), .b({multiplexer_11_out_2, multiplexer_11_out}), .out(fpadder_1_out));
  FPSubtractor fpsubtractor_1 (.a(Base), .b({multiplexer_11_out_2, multiplexer_11_out}), .out(fpsubtractor_1_out));
  // FPNegator fpnegator_1: pin names not known; wires that end beside it: {multiplexer_11_out_2, multiplexer_11_out}, fpnegator_1_p2
  FPMultiplier fpmultiplier_1 (.a(Base), .b({multiplexer_11_out_2, multiplexer_11_out}), .out(fpmultiplier_1_out));
  FPDivider fpdivider_1 (.a(Base), .b({multiplexer_11_out_2, multiplexer_11_out}), .out(fpdivider_1_out));
  // FPToInt #(.width(32)) fptoint_1: pin names not known; wires that end beside it: {multiplexer_11_out_2, multiplexer_11_out}, fptoint_1_p2
  Multiplier #(.width(32)) multiplier_1 (
    .a(Base), .b({multiplexer_11_out_2, multiplexer_11_out}), .out(multiplier_1_out));  // open: cin, cout
  Divider #(.width(32)) divider_1 (
    .a(Base), .b({multiplexer_11_out_2, multiplexer_11_out}), .out(divider_1_out), .rem(divider_1_rem));  // open: upper
  Shifter #(.shift("lr"), .width(32)) shifter_1 (.in(Base), .\dist (multiplexer_11_out), .out(shifter_1_out));
  Shifter #(.width(32)) shifter_2 (.in(Base), .\dist (multiplexer_11_out), .out(shifter_2_out));
  Shifter #(.shift("ar"), .width(32)) shifter_3 (.in(Base), .\dist (multiplexer_11_out), .out(shifter_3_out));
  Shifter #(.shift("rl"), .width(32)) shifter_4 (.in(Base), .\dist (multiplexer_11_out), .out(shifter_4_out));
  Shifter #(.shift("rr"), .width(32)) shifter_5 (.in(Base), .\dist (multiplexer_11_out), .out(shifter_5_out));
  assign Offset24 = {{8{in_2}}, {in_2, Code24}};  // Bit_Extender bit_extender_1
  MyAdder myadder_1 (
    .A({multiplexer_11_out_2, multiplexer_11_out}), .B(multiplexer_12_out), .H(in_1), .W(in_2),
    .Cin(controlled_buffer_6_out), .Cout(comparator_1_eq[3]), .V(comparator_1_eq[2]), .Add(myadder_1_add));
  or or_10 (in_1, in_2, Code24[22]);
  and and_25 (and_25_out, Code24[20], ~Code24[19], ~Code24[18]);  // AND_Gate
  assign Const8 = {{24{Code24[15]}}, Code24[15:8]};  // Bit_Extender bit_extender_2
  assign controlled_buffer_6_out = and_26_out ? CVNZ[3] : 1'bz;  // Controlled_Buffer controlled_buffer_6
  Multiplexer #(.select(5), .width(32)) multiplexer_13 (
    .in0({multiplexer_11_out_2, multiplexer_11_out}), .in1(undriven_9), .in2(undriven_9),
    .in3(myadder_1_add), .in4(negator_1_out), .in5(undriven_9), .in6(undriven_9), .in7(undriven_9),
    .in8(not_6_out), .in10(and_24_out), .in11(and_24_out), .in13(or_9_out), .in14(xor_3_out),
    .in15(xor_3_out), .in16(inttofp_1_p2), .in17(fpadder_1_out), .in18(fpsubtractor_1_out),
    .in19(fpnegator_1_p2), .in20(fpmultiplier_1_out), .in21(fpdivider_1_out), .in23(fptoint_1_p2),
    .in24(multiplier_1_out), .in25(divider_1_out), .in26(divider_1_rem), .in27(shifter_1_out),
    .in28(shifter_2_out), .in29(shifter_3_out), .in30(shifter_4_out), .in31(shifter_5_out),
    .out(multiplexer_13_out), .sel(Code24[20:16]));  // open: in9, in12, in22
  and and_26 (and_26_out, ~Code24[20], ~Code24[19], Code24[17], ~Code24[16]);  // AND_Gate
  assign Data = and_27_out ? multiplexer_13_out : 32'bz;  // Controlled_Buffer controlled_buffer_7
  and and_27 (and_27_out, Clk, ALU);
  and and_28 (Cmp, ALU, ~Code24[20], Code24[16], Code24[17]);  // AND_Gate
  Comparator #(.width(32)) comparator_1 (
    .a(Data), .b({32{1'b0}}), .eq(comparator_1_eq[0]), .lt(comparator_1_eq[1]));  // open: gt
  Register #(.trigger("falling"), .width(4)) register_23 (
    .D(comparator_1_eq), .en(or_11_out), .clk(Clk), .Q(CVNZ), .clr(Reset));
  or or_11 (or_11_out, Cmp, F);

  // Other names for the same wires on the sheet: Rd[3:0] = Code24[3:0]; Rs[3:0] = Code24[7:4]; I = Code24[21];
  //   Code24[23] = in_2; W = in_2; Rs2[3:0] = Code24[11:8]; H = in_1; Op5[4:0] = Code24[20:16]; D = Code24[20]
endmodule

module MyAdder (
  input  [31:0] A,
  input  [31:0] B,
  input  Cin,
  input  H,
  input  W,
  output [31:0] Add,
  output V,
  output Cout
);

  wire adder_1_cout, adder_2_cout, adder_3_cout, adder_4_cout, adder_5_cout, adder_6_cout, xor_1_out,
       xor_2_out, xor_3_out;

  Adder #(.width(7)) adder_1 (.a(A[6:0]), .b(B[6:0]), .out(Add[6:0]), .cin(Cin), .cout(adder_1_cout));
  Adder #(.width(1)) adder_2 (.a(A[7]), .b(B[7]), .out(Add[7]), .cin(adder_1_cout), .cout(adder_2_cout));
  Adder #(.width(7)) adder_3 (.a(A[14:8]), .b(B[14:8]), .out(Add[14:8]), .cin(adder_2_cout), .cout(adder_3_cout));
  Adder #(.width(1)) adder_4 (.a(A[15]), .b(B[15]), .out(Add[15]), .cin(adder_3_cout), .cout(adder_4_cout));
  Adder #(.width(15)) adder_5 (.a(A[30:16]), .b(B[30:16]), .out(Add[30:16]), .cin(adder_4_cout), .cout(adder_5_cout));
  Adder #(.width(1)) adder_6 (.a(A[31]), .b(B[31]), .out(Add[31]), .cin(adder_5_cout), .cout(adder_6_cout));
  xor xor_1 (xor_1_out, adder_6_cout, adder_5_cout);
  Multiplexer #(.select(2)) multiplexer_1 (
    .in0(adder_2_cout), .in1(adder_4_cout), .in2(adder_6_cout), .in3(adder_6_cout), .out(Cout), .sel({W, H}));
  xor xor_2 (xor_2_out, adder_2_cout, adder_1_cout);
  xor xor_3 (xor_3_out, adder_4_cout, adder_3_cout);
  Multiplexer #(.select(2)) multiplexer_2 (
    .in0(xor_2_out), .in1(xor_3_out), .in2(xor_1_out), .in3(xor_1_out), .out(V), .sel({W, H}));
endmodule
